// Logisim project BarrelShifter.circ as structural Verilog: 1 circuit, main circuit main
module main (
);

  wire dipswitch_2_p1, dipswitch_2_p2, dipswitch_2_p3, dipswitch_2_p4, dipswitch_2_p5, dipswitch_2_p6,
       dipswitch_2_p7, dipswitch_2_p8, dipswitch_4_p1, dipswitch_4_p2, dipswitch_4_p3, dipswitch_4_p4,
       multiplexer_1_out, multiplexer_2_out, multiplexer_3_out, multiplexer_4_out, multiplexer_5_out,
       multiplexer_6_out, multiplexer_7_out, multiplexer_8_out, multiplexer_9_out, multiplexer_10_out,
       multiplexer_11_out, multiplexer_12_out;
  wire [2:0] dipswitch_1_p3, dipswitch_3_p3;

  // DipSwitch #(.number(3)) dipswitch_1: pin names not known; wires that end beside it: dipswitch_1_p3[2], dipswitch_1_p3[1], dipswitch_1_p3[0]
  // DipSwitch dipswitch_2: pin names not known; wires that end beside it: dipswitch_2_p1, dipswitch_2_p2, dipswitch_2_p3, dipswitch_2_p4, dipswitch_2_p5, dipswitch_2_p6, dipswitch_2_p7, dipswitch_2_p8
  Multiplexer #(.select(3)) multiplexer_1 (
    .in0(dipswitch_2_p7), .in1(dipswitch_2_p8), .in2(1'b0), .in3(1'b0), .in4(1'b0), .in5(1'b0), .in6(1'b0),
    .in7(1'b0), .out(multiplexer_1_out), .sel(dipswitch_1_p3));
  LED led_1 (.in(multiplexer_1_out));
  LED led_2 (.in(multiplexer_1_out));
  Multiplexer #(.select(3)) multiplexer_2 (
    .in0(dipswitch_2_p8), .in1(1'b0), .in2(1'b0), .in3(1'b0), .in4(1'b0), .in5(1'b0), .in6(1'b0), .in7(1'b0),
    .out(multiplexer_2_out), .sel(dipswitch_1_p3));
  LED led_3 (.in(multiplexer_2_out));
  Multiplexer #(.select(3)) multiplexer_3 (
    .in0(dipswitch_2_p1), .in1(dipswitch_2_p2), .in2(dipswitch_2_p3), .in3(dipswitch_2_p4),
    .in4(dipswitch_2_p5), .in5(dipswitch_2_p6), .in6(dipswitch_2_p7), .in7(dipswitch_2_p8),
    .out(multiplexer_3_out), .sel(dipswitch_1_p3));
  Multiplexer #(.select(3)) multiplexer_4 (
    .in0(dipswitch_2_p2), .in1(dipswitch_2_p3), .in2(dipswitch_2_p4), .in3(dipswitch_2_p5),
    .in4(dipswitch_2_p6), .in5(dipswitch_2_p7), .in6(dipswitch_2_p8), .in7(1'b0), .out(multiplexer_4_out),
    .sel(dipswitch_1_p3));
  Multiplexer #(.select(3)) multiplexer_5 (
    .in0(dipswitch_2_p3), .in1(dipswitch_2_p4), .in2(dipswitch_2_p5), .in3(dipswitch_2_p6),
    .in4(dipswitch_2_p7), .in5(dipswitch_2_p8), .in6(1'b0), .in7(1'b0), .out(multiplexer_5_out),
    .sel(dipswitch_1_p3));
  Multiplexer #(.select(3)) multiplexer_6 (
    .in0(dipswitch_2_p4), .in1(dipswitch_2_p5), .in2(dipswitch_2_p6), .in3(dipswitch_2_p7),
    .in4(dipswitch_2_p8), .in5(1'b0), .in6(1'b0), .in7(1'b0), .out(multiplexer_6_out), .sel(dipswitch_1_p3));
  Multiplexer #(.select(3)) multiplexer_7 (
    .in0(dipswitch_2_p5), .in1(dipswitch_2_p6), .in2(dipswitch_2_p7), .in3(dipswitch_2_p8), .in4(1'b0),
    .in5(1'b0), .in6(1'b0), .in7(1'b0), .out(multiplexer_7_out), .sel(dipswitch_1_p3));
  Multiplexer #(.select(3)) multiplexer_8 (
    .in0(dipswitch_2_p6), .in1(dipswitch_2_p7), .in2(dipswitch_2_p8), .in3(1'b0), .in4(1'b0), .in5(1'b0),
    .in6(1'b0), .in7(1'b0), .out(multiplexer_8_out), .sel(dipswitch_1_p3));
  LED led_4 (.in(multiplexer_3_out));
  LED led_5 (.in(multiplexer_3_out));
  LED led_6 (.in(multiplexer_4_out));
  LED led_7 (.in(multiplexer_4_out));
  LED led_8 (.in(multiplexer_5_out));
  LED led_9 (.in(multiplexer_5_out));
  LED led_10 (.in(multiplexer_6_out));
  LED led_11 (.in(multiplexer_6_out));
  LED led_12 (.in(multiplexer_7_out));
  LED led_13 (.in(multiplexer_8_out));
  LED led_14 (.in(multiplexer_8_out));
  // DipSwitch #(.number(3)) dipswitch_3: pin names not known; wires that end beside it: dipswitch_3_p3[2], dipswitch_3_p3[1], dipswitch_3_p3[0]
  // DipSwitch #(.number(4)) dipswitch_4: pin names not known; wires that end beside it: dipswitch_4_p1, dipswitch_4_p2, dipswitch_4_p3, dipswitch_4_p4
  Multiplexer #(.select(3)) multiplexer_9 (
    .in0(dipswitch_4_p1), .in1(dipswitch_4_p2), .in2(dipswitch_4_p3), .in3(dipswitch_4_p4),
    .in4(dipswitch_4_p1), .in5(dipswitch_4_p1), .in6(dipswitch_4_p1), .in7(dipswitch_4_p1),
    .out(multiplexer_9_out), .sel(dipswitch_3_p3));
  LED led_15 (.in(multiplexer_9_out));
  Multiplexer #(.select(3)) multiplexer_10 (
    .in0(dipswitch_4_p2), .in1(dipswitch_4_p3), .in2(dipswitch_4_p4), .in3(1'b0), .in4(dipswitch_4_p2),
    .in5(dipswitch_4_p1), .in6(dipswitch_4_p1), .in7(dipswitch_4_p1), .out(multiplexer_10_out),
    .sel(dipswitch_3_p3));
  LED led_16 (.in(multiplexer_10_out));
  LED led_17 (.in(multiplexer_10_out));
  Multiplexer #(.select(3)) multiplexer_11 (
    .in0(dipswitch_4_p3), .in1(dipswitch_4_p4), .in2(1'b0), .in3(1'b0), .in4(dipswitch_4_p3),
    .in5(dipswitch_4_p2), .in6(dipswitch_4_p1), .in7(dipswitch_4_p1), .out(multiplexer_11_out),
    .sel(dipswitch_3_p3));
  LED led_18 (.in(multiplexer_11_out));
  LED led_19 (.in(multiplexer_11_out));
  Multiplexer #(.select(3)) multiplexer_12 (
    .in0(dipswitch_4_p4), .in1(1'b0), .in2(1'b0), .in3(1'b0), .in4(dipswitch_4_p4), .in5(dipswitch_4_p3),
    .in6(dipswitch_4_p2), .in7(dipswitch_4_p1), .out(multiplexer_12_out), .sel(dipswitch_3_p3));
  LED led_20 (.in(multiplexer_12_out));

  // Notes on the sheet:
  //   1
  //   0
  //   5
  //   4
  //   3
  //   7
  //   6
  //   2
  //   3
  //   2
  //   1
  //   0
endmodule
