// Logisim project MIPS.circ as structural Verilog: 12 circuits, main circuit main
module main (
  input  in_1,
  input  in_2,
  input  in_3
);

  wire and_1_out, and_2_out, clock_1_out, comp_1_out_3, not_1_out, opdecoder_1_beq, opdecoder_1_bne,
       opdecoder_1_cin, opdecoder_1_imm, opdecoder_1_jmp, opdecoder_1_lw, opdecoder_1_r_l, opdecoder_1_shft,
       opdecoder_1_sw, or_1_out, or_2_out;
  wire [1:0] opdecoder_1_sign;
  wire [2:0] opdecoder_1_sel;
  wire [4:0] opdecoder_1_shamt;
  wire [7:0] rom_1_p2, rom_1_p3, rom_1_p4, rom_1_p5;
  wire [23:0] b3224_1_out_2, b3224_2_out_2;
  wire [31:0] alu_1_dbus, alu_2_dbus, alu_3_dbus, barrelshifter_1_shout, barrelshifter_2_shout,
       barrelshifter_3_shout, extend_1_out_2, multiplexer_1_out, multiplexer_2_out, multiplexer_3_out,
       multiplexer_4_out, multiplexer_5_out, multiplexer_6_out, opdecoder_1_asel, opdecoder_1_bsel,
       opdecoder_1_dsel, ram_1_dout, register_1_q, register_32x32b_1_abus, register_32x32b_1_bbus,
       retractor_1_out_2;

  Clock clock_1 (.out(clock_1_out));
  Multiplexer #(.width(32)) multiplexer_1 (
    .in0(alu_1_dbus), .in1(barrelshifter_1_shout), .out(multiplexer_1_out), .sel(opdecoder_1_jmp));
  Multiplexer #(.width(32)) multiplexer_2 (
    .in0(multiplexer_1_out), .in1(alu_2_dbus), .out(multiplexer_2_out), .sel(or_2_out));
  Register #(.width(32)) register_1 (.D(multiplexer_2_out), .en(1'b1), .clk(clock_1_out), .Q(register_1_q), .clr(in_1));
  b3224 b3224_1 (.in_1(register_1_q), .out_2(b3224_1_out_2));
  // ROM #(.addrWidth(24), .line("quad")) rom_1: pin names not known; wires that end beside it: b3224_1_out_2, rom_1_p2, rom_1_p3, rom_1_p4, rom_1_p5
  ALU alu_1 (.Cin(in_2), .Sel(3'b010), .Abus(register_1_q), .Bbus(32'h4), .Dbus(alu_1_dbus));  // open: Zero, Cout, Ovf
  OpDecoder opdecoder_1 (
    .Ibus({rom_1_p5, rom_1_p4, rom_1_p3, rom_1_p2}), .SHAMT(opdecoder_1_shamt), .LW(opdecoder_1_lw),
    .SW(opdecoder_1_sw), .Cin(opdecoder_1_cin), .BEQ(opdecoder_1_beq), .BNE(opdecoder_1_bne),
    .JMP(opdecoder_1_jmp), .SHFT(opdecoder_1_shft), .R_L(opdecoder_1_r_l), .Sign(opdecoder_1_sign),
    .Sel(opdecoder_1_sel), .IMM(opdecoder_1_imm), .Bsel(opdecoder_1_bsel), .Dsel(opdecoder_1_dsel),
    .Asel(opdecoder_1_asel));
  Retractor retractor_1 (.in_1({rom_1_p5, rom_1_p4, rom_1_p3, rom_1_p2}), .out_2(retractor_1_out_2));
  Extend extend_1 (.in_1({rom_1_p5, rom_1_p4, rom_1_p3, rom_1_p2}), .out_2(extend_1_out_2));
  Barrelshifter barrelshifter_1 (
    .SHIN(retractor_1_out_2), .SIGN(2'b00), .L_R(1'b0), .SHAMT(5'b00010), .SHOUT(barrelshifter_1_shout));
  Register_32x32b register_32x32b_1 (
    .Asel(opdecoder_1_asel), .Bsel(opdecoder_1_bsel), .Dsel(multiplexer_4_out), .rst(in_1),
    .clk(clock_1_out), .NWE(or_1_out), .Dbus(multiplexer_6_out), .Abus(register_32x32b_1_abus),
    .Bbus(register_32x32b_1_bbus));
  Multiplexer #(.width(32)) multiplexer_3 (
    .in0(register_32x32b_1_bbus), .in1(extend_1_out_2), .out(multiplexer_3_out), .sel(opdecoder_1_imm));
  Multiplexer #(.width(32)) multiplexer_4 (
    .in0(opdecoder_1_dsel), .in1(32'h1), .out(multiplexer_4_out), .sel(or_1_out));
  or or_1 (or_1_out, opdecoder_1_bne, opdecoder_1_beq, opdecoder_1_sw, opdecoder_1_jmp);
  Barrelshifter barrelshifter_2 (
    .SHIN(register_32x32b_1_bbus), .SIGN(opdecoder_1_sign), .L_R(opdecoder_1_r_l), .SHAMT(opdecoder_1_shamt),
    .SHOUT(barrelshifter_2_shout));
  Barrelshifter barrelshifter_3 (
    .SHIN(extend_1_out_2), .SIGN(2'b00), .L_R(1'b0), .SHAMT(5'b00010), .SHOUT(barrelshifter_3_shout));
  ALU alu_2 (
    .Cin(in_3), .Sel(3'b010), .Abus(register_1_q), .Bbus(barrelshifter_3_shout), .Dbus(alu_2_dbus));  // open: Zero, Cout, Ovf
  Comp comp_1 (.in_2(register_32x32b_1_bbus), .in_1(register_32x32b_1_abus), .out_3(comp_1_out_3));
  not not_1 (not_1_out, comp_1_out_3);
  ALU alu_3 (
    .Cin(opdecoder_1_cin), .Sel(opdecoder_1_sel), .Abus(register_32x32b_1_abus), .Bbus(multiplexer_3_out),
    .Dbus(alu_3_dbus));  // open: Zero, Cout, Ovf
  and and_1 (and_1_out, opdecoder_1_beq, comp_1_out_3);
  and and_2 (and_2_out, not_1_out, opdecoder_1_bne);
  or or_2 (or_2_out, and_1_out, and_2_out);
  Multiplexer #(.width(32)) multiplexer_5 (
    .in0(alu_3_dbus), .in1(barrelshifter_2_shout), .out(multiplexer_5_out), .sel(opdecoder_1_shft));
  b3224 b3224_2 (.in_1(multiplexer_5_out), .out_2(b3224_2_out_2));
  RAM #(.addrWidth(24), .dataWidth(32)) ram_1 (
    .addr(b3224_2_out_2), .we(opdecoder_1_sw), .oe(opdecoder_1_lw), .clk(clock_1_out),
    .din(register_32x32b_1_bbus), .dout(ram_1_dout));
  Multiplexer #(.width(32)) multiplexer_6 (
    .in0(multiplexer_5_out), .in1(ram_1_dout), .out(multiplexer_6_out), .sel(opdecoder_1_lw));

  // Notes on the sheet:
  //   contents of rom_1 (hex, n*v repeats v):
  //   4*0 a 0 1 88 a8 10 1 0 3 0 2 c8
  //   Instruction memory
  //   OP decoder
  //   Register
endmodule

module Register_32x32b (
  input  NWE,
  input  [31:0] Asel,
  input  [31:0] Bsel,
  input  [31:0] Dbus,
  input  rst,
  input  clk,
  input  [31:0] Dsel,
  output [31:0] Abus,
  output [31:0] Bbus
);

  wire and_1_out, and_2_out, and_3_out, and_4_out, and_5_out, and_6_out, and_7_out, and_8_out, and_9_out,
       and_10_out, and_11_out, and_12_out, and_13_out, and_14_out, and_15_out, and_16_out, and_17_out,
       and_18_out, and_19_out, and_20_out, and_21_out, and_22_out, and_23_out, and_24_out, and_25_out,
       and_26_out, and_27_out, and_28_out, and_29_out, and_30_out, and_31_out, d_ff_1_q, not_1_out, undriven;
  wire [31:0] register_1_q, register_2_q, register_3_q, register_4_q, register_5_q, register_6_q,
       register_7_q, register_8_q, register_9_q, register_10_q, register_11_q, register_12_q, register_13_q,
       register_14_q, register_15_q, register_16_q, register_17_q, register_18_q, register_19_q,
       register_20_q, register_21_q, register_22_q, register_23_q, register_24_q, register_25_q,
       register_26_q, register_27_q, register_28_q, register_29_q, register_30_q, register_31_q;

  not not_1 (not_1_out, NWE);
  and and_1 (and_1_out, clk, Dsel[1]);
  and and_2 (and_2_out, clk, Dsel[2]);
  and and_3 (and_3_out, clk, Dsel[3]);
  and and_4 (and_4_out, clk, Dsel[4]);
  and and_5 (and_5_out, clk, Dsel[5]);
  and and_6 (and_6_out, clk, Dsel[6]);
  and and_7 (and_7_out, clk, Dsel[7]);
  and and_8 (and_8_out, clk, Dsel[8]);
  and and_9 (and_9_out, clk, Dsel[9]);
  and and_10 (and_10_out, clk, Dsel[10]);
  and and_11 (and_11_out, clk, Dsel[11]);
  and and_12 (and_12_out, clk, Dsel[12]);
  and and_13 (and_13_out, clk, Dsel[13]);
  and and_14 (and_14_out, clk, Dsel[14]);
  and and_15 (and_15_out, clk, Dsel[15]);
  and and_16 (and_16_out, clk, Dsel[16]);
  and and_17 (and_17_out, clk, Dsel[17]);
  and and_18 (and_18_out, clk, Dsel[18]);
  and and_19 (and_19_out, clk, Dsel[19]);
  and and_20 (and_20_out, clk, Dsel[20]);
  and and_21 (and_21_out, clk, Dsel[21]);
  and and_22 (and_22_out, clk, Dsel[22]);
  and and_23 (and_23_out, clk, Dsel[23]);
  and and_24 (and_24_out, clk, Dsel[24]);
  and and_25 (and_25_out, clk, Dsel[25]);
  and and_26 (and_26_out, clk, Dsel[26]);
  and and_27 (and_27_out, clk, Dsel[27]);
  and and_28 (and_28_out, clk, Dsel[28]);
  and and_29 (and_29_out, clk, Dsel[29]);
  and and_30 (and_30_out, clk, Dsel[30]);
  and and_31 (and_31_out, clk, Dsel[31]);
  D_Flip_Flop d_ff_1 (.D(not_1_out), .clk(clk), .Q(d_ff_1_q), .preset(rst), .reset(undriven));  // open: Qn
  Register #(.trigger("falling"), .width(32)) register_1 (
    .D(Dbus), .en(d_ff_1_q), .clk(and_1_out), .Q(register_1_q), .clr(rst));
  Register #(.trigger("falling"), .width(32)) register_2 (
    .D(Dbus), .en(d_ff_1_q), .clk(and_2_out), .Q(register_2_q), .clr(rst));
  Register #(.trigger("falling"), .width(32)) register_3 (
    .D(Dbus), .en(d_ff_1_q), .clk(and_3_out), .Q(register_3_q), .clr(rst));
  Register #(.trigger("falling"), .width(32)) register_4 (
    .D(Dbus), .en(d_ff_1_q), .clk(and_4_out), .Q(register_4_q), .clr(rst));
  Register #(.trigger("falling"), .width(32)) register_5 (
    .D(Dbus), .en(d_ff_1_q), .clk(and_5_out), .Q(register_5_q), .clr(rst));
  Register #(.trigger("falling"), .width(32)) register_6 (
    .D(Dbus), .en(d_ff_1_q), .clk(and_6_out), .Q(register_6_q), .clr(rst));
  Register #(.trigger("falling"), .width(32)) register_7 (
    .D(Dbus), .en(d_ff_1_q), .clk(and_7_out), .Q(register_7_q), .clr(rst));
  Register #(.trigger("falling"), .width(32)) register_8 (
    .D(Dbus), .en(d_ff_1_q), .clk(and_8_out), .Q(register_8_q), .clr(rst));
  Register #(.trigger("falling"), .width(32)) register_9 (
    .D(Dbus), .en(d_ff_1_q), .clk(and_9_out), .Q(register_9_q), .clr(rst));
  Register #(.trigger("falling"), .width(32)) register_10 (
    .D(Dbus), .en(d_ff_1_q), .clk(and_10_out), .Q(register_10_q), .clr(rst));
  Register #(.trigger("falling"), .width(32)) register_11 (
    .D(Dbus), .en(d_ff_1_q), .clk(and_11_out), .Q(register_11_q), .clr(rst));
  Register #(.trigger("falling"), .width(32)) register_12 (
    .D(Dbus), .en(d_ff_1_q), .clk(and_12_out), .Q(register_12_q), .clr(rst));
  Register #(.trigger("falling"), .width(32)) register_13 (
    .D(Dbus), .en(d_ff_1_q), .clk(and_13_out), .Q(register_13_q), .clr(rst));
  Register #(.trigger("falling"), .width(32)) register_14 (
    .D(Dbus), .en(d_ff_1_q), .clk(and_14_out), .Q(register_14_q), .clr(rst));
  Register #(.trigger("falling"), .width(32)) register_15 (
    .D(Dbus), .en(d_ff_1_q), .clk(and_15_out), .Q(register_15_q), .clr(rst));
  Register #(.trigger("falling"), .width(32)) register_16 (
    .D(Dbus), .en(d_ff_1_q), .clk(and_16_out), .Q(register_16_q), .clr(rst));
  Register #(.trigger("falling"), .width(32)) register_17 (
    .D(Dbus), .en(d_ff_1_q), .clk(and_17_out), .Q(register_17_q), .clr(rst));
  Register #(.trigger("falling"), .width(32)) register_18 (
    .D(Dbus), .en(d_ff_1_q), .clk(and_18_out), .Q(register_18_q), .clr(rst));
  Register #(.trigger("falling"), .width(32)) register_19 (
    .D(Dbus), .en(d_ff_1_q), .clk(and_19_out), .Q(register_19_q), .clr(rst));
  Register #(.trigger("falling"), .width(32)) register_20 (
    .D(Dbus), .en(d_ff_1_q), .clk(and_20_out), .Q(register_20_q), .clr(rst));
  Register #(.trigger("falling"), .width(32)) register_21 (
    .D(Dbus), .en(d_ff_1_q), .clk(and_21_out), .Q(register_21_q), .clr(rst));
  Register #(.trigger("falling"), .width(32)) register_22 (
    .D(Dbus), .en(d_ff_1_q), .clk(and_22_out), .Q(register_22_q), .clr(rst));
  Register #(.trigger("falling"), .width(32)) register_23 (
    .D(Dbus), .en(d_ff_1_q), .clk(and_23_out), .Q(register_23_q), .clr(rst));
  Register #(.trigger("falling"), .width(32)) register_24 (
    .D(Dbus), .en(d_ff_1_q), .clk(and_24_out), .Q(register_24_q), .clr(rst));
  Register #(.trigger("falling"), .width(32)) register_25 (
    .D(Dbus), .en(d_ff_1_q), .clk(and_25_out), .Q(register_25_q), .clr(rst));
  Register #(.trigger("falling"), .width(32)) register_26 (
    .D(Dbus), .en(d_ff_1_q), .clk(and_26_out), .Q(register_26_q), .clr(rst));
  Register #(.trigger("falling"), .width(32)) register_27 (
    .D(Dbus), .en(d_ff_1_q), .clk(and_27_out), .Q(register_27_q), .clr(rst));
  Register #(.trigger("falling"), .width(32)) register_28 (
    .D(Dbus), .en(d_ff_1_q), .clk(and_28_out), .Q(register_28_q), .clr(rst));
  Register #(.trigger("falling"), .width(32)) register_29 (
    .D(Dbus), .en(d_ff_1_q), .clk(and_29_out), .Q(register_29_q), .clr(rst));
  Register #(.trigger("falling"), .width(32)) register_30 (
    .D(Dbus), .en(d_ff_1_q), .clk(and_30_out), .Q(register_30_q), .clr(rst));
  Register #(.trigger("falling"), .width(32)) register_31 (
    .D(Dbus), .en(d_ff_1_q), .clk(and_31_out), .Q(register_31_q), .clr(rst));
  assign Abus = Asel[0] ? {32{1'b0}} : 32'bz;  // Controlled_Buffer controlled_buffer_1
  assign Bbus = Bsel[0] ? {32{1'b0}} : 32'bz;  // Controlled_Buffer controlled_buffer_2
  assign Abus = Asel[1] ? register_1_q : 32'bz;  // Controlled_Buffer controlled_buffer_3
  assign Bbus = Bsel[1] ? register_1_q : 32'bz;  // Controlled_Buffer controlled_buffer_4
  assign Abus = Asel[2] ? register_2_q : 32'bz;  // Controlled_Buffer controlled_buffer_5
  assign Bbus = Bsel[2] ? register_2_q : 32'bz;  // Controlled_Buffer controlled_buffer_6
  assign Abus = Asel[3] ? register_3_q : 32'bz;  // Controlled_Buffer controlled_buffer_7
  assign Bbus = Bsel[3] ? register_3_q : 32'bz;  // Controlled_Buffer controlled_buffer_8
  assign Abus = Asel[4] ? register_4_q : 32'bz;  // Controlled_Buffer controlled_buffer_9
  assign Bbus = Bsel[4] ? register_4_q : 32'bz;  // Controlled_Buffer controlled_buffer_10
  assign Abus = Asel[5] ? register_5_q : 32'bz;  // Controlled_Buffer controlled_buffer_11
  assign Bbus = Bsel[5] ? register_5_q : 32'bz;  // Controlled_Buffer controlled_buffer_12
  assign Abus = Asel[6] ? register_6_q : 32'bz;  // Controlled_Buffer controlled_buffer_13
  assign Bbus = Bsel[6] ? register_6_q : 32'bz;  // Controlled_Buffer controlled_buffer_14
  assign Abus = Asel[7] ? register_7_q : 32'bz;  // Controlled_Buffer controlled_buffer_15
  assign Bbus = Bsel[7] ? register_7_q : 32'bz;  // Controlled_Buffer controlled_buffer_16
  assign Abus = Asel[8] ? register_8_q : 32'bz;  // Controlled_Buffer controlled_buffer_17
  assign Bbus = Bsel[8] ? register_8_q : 32'bz;  // Controlled_Buffer controlled_buffer_18
  assign Abus = Asel[9] ? register_9_q : 32'bz;  // Controlled_Buffer controlled_buffer_19
  assign Bbus = Bsel[9] ? register_9_q : 32'bz;  // Controlled_Buffer controlled_buffer_20
  assign Abus = Asel[10] ? register_10_q : 32'bz;  // Controlled_Buffer controlled_buffer_21
  assign Bbus = Bsel[10] ? register_10_q : 32'bz;  // Controlled_Buffer controlled_buffer_22
  assign Abus = Asel[11] ? register_11_q : 32'bz;  // Controlled_Buffer controlled_buffer_23
  assign Bbus = Bsel[11] ? register_11_q : 32'bz;  // Controlled_Buffer controlled_buffer_24
  assign Abus = Asel[12] ? register_12_q : 32'bz;  // Controlled_Buffer controlled_buffer_25
  assign Bbus = Bsel[12] ? register_12_q : 32'bz;  // Controlled_Buffer controlled_buffer_26
  assign Abus = Asel[13] ? register_13_q : 32'bz;  // Controlled_Buffer controlled_buffer_27
  assign Bbus = Bsel[13] ? register_13_q : 32'bz;  // Controlled_Buffer controlled_buffer_28
  assign Abus = Asel[14] ? register_14_q : 32'bz;  // Controlled_Buffer controlled_buffer_29
  assign Bbus = Bsel[14] ? register_14_q : 32'bz;  // Controlled_Buffer controlled_buffer_30
  assign Abus = Asel[15] ? register_15_q : 32'bz;  // Controlled_Buffer controlled_buffer_31
  assign Bbus = Bsel[15] ? register_15_q : 32'bz;  // Controlled_Buffer controlled_buffer_32
  assign Abus = Asel[16] ? register_16_q : 32'bz;  // Controlled_Buffer controlled_buffer_33
  assign Bbus = Bsel[16] ? register_16_q : 32'bz;  // Controlled_Buffer controlled_buffer_34
  assign Abus = Asel[17] ? register_17_q : 32'bz;  // Controlled_Buffer controlled_buffer_35
  assign Bbus = Bsel[17] ? register_17_q : 32'bz;  // Controlled_Buffer controlled_buffer_36
  assign Abus = Asel[18] ? register_18_q : 32'bz;  // Controlled_Buffer controlled_buffer_37
  assign Bbus = Bsel[18] ? register_18_q : 32'bz;  // Controlled_Buffer controlled_buffer_38
  assign Abus = Asel[19] ? register_19_q : 32'bz;  // Controlled_Buffer controlled_buffer_39
  assign Bbus = Bsel[19] ? register_19_q : 32'bz;  // Controlled_Buffer controlled_buffer_40
  assign Abus = Asel[20] ? register_20_q : 32'bz;  // Controlled_Buffer controlled_buffer_41
  assign Bbus = Bsel[20] ? register_20_q : 32'bz;  // Controlled_Buffer controlled_buffer_42
  assign Abus = Asel[21] ? register_21_q : 32'bz;  // Controlled_Buffer controlled_buffer_43
  assign Bbus = Bsel[21] ? register_21_q : 32'bz;  // Controlled_Buffer controlled_buffer_44
  assign Abus = Asel[22] ? register_22_q : 32'bz;  // Controlled_Buffer controlled_buffer_45
  assign Bbus = Bsel[22] ? register_22_q : 32'bz;  // Controlled_Buffer controlled_buffer_46
  assign Abus = Asel[23] ? register_23_q : 32'bz;  // Controlled_Buffer controlled_buffer_47
  assign Bbus = Bsel[23] ? register_23_q : 32'bz;  // Controlled_Buffer controlled_buffer_48
  assign Abus = Asel[24] ? register_24_q : 32'bz;  // Controlled_Buffer controlled_buffer_49
  assign Bbus = Bsel[24] ? register_24_q : 32'bz;  // Controlled_Buffer controlled_buffer_50
  assign Abus = Asel[25] ? register_25_q : 32'bz;  // Controlled_Buffer controlled_buffer_51
  assign Bbus = Bsel[25] ? register_25_q : 32'bz;  // Controlled_Buffer controlled_buffer_52
  assign Abus = Asel[26] ? register_26_q : 32'bz;  // Controlled_Buffer controlled_buffer_53
  assign Bbus = Bsel[26] ? register_26_q : 32'bz;  // Controlled_Buffer controlled_buffer_54
  assign Abus = Asel[27] ? register_27_q : 32'bz;  // Controlled_Buffer controlled_buffer_55
  assign Bbus = Bsel[27] ? register_27_q : 32'bz;  // Controlled_Buffer controlled_buffer_56
  assign Abus = Asel[28] ? register_28_q : 32'bz;  // Controlled_Buffer controlled_buffer_57
  assign Bbus = Bsel[28] ? register_28_q : 32'bz;  // Controlled_Buffer controlled_buffer_58
  assign Abus = Asel[29] ? register_29_q : 32'bz;  // Controlled_Buffer controlled_buffer_59
  assign Bbus = Bsel[29] ? register_29_q : 32'bz;  // Controlled_Buffer controlled_buffer_60
  assign Abus = Asel[30] ? register_30_q : 32'bz;  // Controlled_Buffer controlled_buffer_61
  assign Bbus = Bsel[30] ? register_30_q : 32'bz;  // Controlled_Buffer controlled_buffer_62
  assign Abus = Asel[31] ? register_31_q : 32'bz;  // Controlled_Buffer controlled_buffer_63
  assign Bbus = Bsel[31] ? register_31_q : 32'bz;  // Controlled_Buffer controlled_buffer_64
endmodule

module LAC32 (
  input  [31:0] G,
  input  [31:0] P,
  input  Cin,
  output [31:0] Cout,
  output gout,
  output pout
);

  wire and_1_out, and_2_out, and_3_out, and_4_out, and_5_out, and_6_out, and_7_out, and_8_out, and_9_out,
       and_10_out, and_11_out, and_12_out, and_13_out, and_14_out, and_15_out, and_16_out, and_17_out,
       and_18_out, and_19_out, and_20_out, and_21_out, and_22_out, and_23_out, and_24_out, and_25_out,
       and_26_out, and_27_out, and_28_out, and_29_out, and_30_out, and_31_out, and_32_out, and_33_out,
       and_34_out, and_35_out, and_36_out, and_37_out, and_38_out, and_39_out, and_40_out, and_41_out,
       and_42_out, and_43_out, and_44_out, and_45_out, and_46_out, and_47_out, and_48_out, and_49_out,
       and_50_out, and_52_out, and_53_out, and_54_out, and_55_out, and_56_out, and_57_out, and_58_out,
       and_59_out, and_60_out, and_61_out, and_62_out, and_63_out, and_64_out, and_65_out, and_66_out,
       and_67_out, and_68_out, and_69_out, and_70_out, and_71_out, and_72_out, and_73_out, and_74_out,
       and_75_out, and_76_out, and_77_out, and_78_out, and_79_out, and_80_out, and_81_out, and_82_out,
       and_83_out, and_84_out, and_85_out, and_86_out, and_87_out, and_88_out, and_89_out, and_90_out,
       and_91_out, and_92_out, and_93_out, or_2_out, or_4_out, or_6_out, or_8_out, or_10_out, or_12_out,
       or_14_out, or_16_out, or_18_out, or_20_out, or_22_out, or_24_out, or_26_out, or_28_out, or_30_out,
       or_32_out, or_36_out, or_38_out, or_40_out, or_42_out, or_44_out, or_46_out, or_48_out, or_50_out,
       or_52_out, or_54_out, or_56_out, or_58_out, or_60_out, or_62_out;

  or or_1 (Cout[31], and_1_out, G[30]);
  and and_1 (and_1_out, Cout[30], P[30]);
  or or_2 (or_2_out, G[31], and_2_out);
  and and_2 (and_2_out, P[31], G[30]);
  and and_3 (and_3_out, P[31], P[30]);
  or or_3 (Cout[30], and_4_out, or_6_out);
  and and_4 (and_4_out, Cout[28], and_9_out);
  and and_5 (and_5_out, and_3_out, or_6_out);
  or or_4 (or_4_out, or_2_out, and_5_out);
  and and_6 (and_6_out, and_3_out, and_9_out);
  or or_5 (Cout[29], and_7_out, G[28]);
  and and_7 (and_7_out, Cout[28], P[28]);
  and and_8 (and_8_out, P[29], G[28]);
  or or_6 (or_6_out, G[29], and_8_out);
  and and_9 (and_9_out, P[29], P[28]);
  or or_7 (Cout[28], and_10_out, or_12_out);
  and and_10 (and_10_out, Cout[24], and_18_out);
  or or_8 (or_8_out, or_4_out, and_11_out);
  and and_11 (and_11_out, and_6_out, or_12_out);
  and and_12 (and_12_out, and_6_out, and_18_out);
  or or_9 (Cout[27], and_13_out, G[26]);
  and and_13 (and_13_out, Cout[26], P[26]);
  and and_14 (and_14_out, P[27], G[26]);
  or or_10 (or_10_out, G[27], and_14_out);
  and and_15 (and_15_out, P[27], P[26]);
  or or_11 (Cout[26], and_16_out, or_14_out);
  and and_16 (and_16_out, Cout[24], and_21_out);
  and and_17 (and_17_out, and_15_out, or_14_out);
  or or_12 (or_12_out, or_10_out, and_17_out);
  and and_18 (and_18_out, and_15_out, and_21_out);
  or or_13 (Cout[25], and_19_out, G[24]);
  and and_19 (and_19_out, Cout[24], P[24]);
  and and_20 (and_20_out, P[25], G[24]);
  or or_14 (or_14_out, G[25], and_20_out);
  and and_21 (and_21_out, P[25], P[24]);
  or or_15 (Cout[24], and_22_out, or_24_out);
  and and_22 (and_22_out, Cout[16], and_36_out);
  and and_23 (and_23_out, and_12_out, or_24_out);
  or or_16 (or_16_out, or_8_out, and_23_out);
  and and_24 (and_24_out, and_12_out, and_36_out);
  or or_17 (Cout[23], and_25_out, G[22]);
  and and_25 (and_25_out, Cout[22], P[22]);
  or or_18 (or_18_out, G[23], and_26_out);
  and and_26 (and_26_out, P[23], G[22]);
  and and_27 (and_27_out, P[23], P[22]);
  or or_19 (Cout[22], and_28_out, or_22_out);
  and and_28 (and_28_out, Cout[20], and_33_out);
  and and_29 (and_29_out, and_27_out, or_22_out);
  or or_20 (or_20_out, or_18_out, and_29_out);
  and and_30 (and_30_out, and_27_out, and_33_out);
  or or_21 (Cout[21], and_31_out, G[20]);
  and and_31 (and_31_out, Cout[20], P[20]);
  and and_32 (and_32_out, P[21], G[20]);
  or or_22 (or_22_out, G[21], and_32_out);
  and and_33 (and_33_out, P[21], P[20]);
  or or_23 (Cout[20], and_34_out, or_28_out);
  and and_34 (and_34_out, Cout[16], and_42_out);
  or or_24 (or_24_out, or_20_out, and_35_out);
  and and_35 (and_35_out, and_30_out, or_28_out);
  and and_36 (and_36_out, and_30_out, and_42_out);
  or or_25 (Cout[19], and_37_out, G[18]);
  and and_37 (and_37_out, Cout[18], P[18]);
  and and_38 (and_38_out, P[19], G[18]);
  or or_26 (or_26_out, G[19], and_38_out);
  and and_39 (and_39_out, P[19], P[18]);
  or or_27 (Cout[18], and_40_out, or_30_out);
  and and_40 (and_40_out, Cout[16], and_45_out);
  and and_41 (and_41_out, and_39_out, or_30_out);
  or or_28 (or_28_out, or_26_out, and_41_out);
  and and_42 (and_42_out, and_39_out, and_45_out);
  or or_29 (Cout[17], and_43_out, G[16]);
  and and_43 (and_43_out, Cout[16], P[16]);
  and and_44 (and_44_out, P[17], G[16]);
  or or_30 (or_30_out, G[17], and_44_out);
  and and_45 (and_45_out, P[17], P[16]);
  or or_31 (Cout[15], and_46_out, G[14]);
  and and_46 (and_46_out, Cout[14], P[14]);
  or or_32 (or_32_out, G[15], and_48_out);
  or or_33 (Cout[16], and_47_out, or_48_out);
  and and_47 (and_47_out, Cin, and_72_out);
  or or_34 (gout, or_16_out, and_50_out);
  and and_48 (and_48_out, P[15], G[14]);
  and and_49 (and_49_out, P[15], P[14]);
  and and_50 (and_50_out, and_24_out, or_48_out);
  and and_51 (pout, and_24_out, and_72_out);
  or or_35 (Cout[14], and_52_out, or_38_out);
  and and_52 (and_52_out, Cout[12], and_57_out);
  and and_53 (and_53_out, and_49_out, or_38_out);
  or or_36 (or_36_out, or_32_out, and_53_out);
  and and_54 (and_54_out, and_49_out, and_57_out);
  or or_37 (Cout[13], and_55_out, G[12]);
  and and_55 (and_55_out, Cout[12], P[12]);
  and and_56 (and_56_out, P[13], G[12]);
  or or_38 (or_38_out, G[13], and_56_out);
  and and_57 (and_57_out, P[13], P[12]);
  or or_39 (Cout[12], and_58_out, or_44_out);
  and and_58 (and_58_out, Cout[8], and_66_out);
  or or_40 (or_40_out, or_36_out, and_59_out);
  and and_59 (and_59_out, and_54_out, or_44_out);
  and and_60 (and_60_out, and_54_out, and_66_out);
  or or_41 (Cout[11], and_61_out, G[10]);
  and and_61 (and_61_out, Cout[10], P[10]);
  and and_62 (and_62_out, P[11], G[10]);
  or or_42 (or_42_out, G[11], and_62_out);
  and and_63 (and_63_out, P[11], P[10]);
  or or_43 (Cout[10], and_64_out, or_46_out);
  and and_64 (and_64_out, Cout[8], and_69_out);
  and and_65 (and_65_out, and_63_out, or_46_out);
  or or_44 (or_44_out, or_42_out, and_65_out);
  and and_66 (and_66_out, and_63_out, and_69_out);
  or or_45 (Cout[9], and_67_out, G[8]);
  and and_67 (and_67_out, Cout[8], P[8]);
  and and_68 (and_68_out, P[9], G[8]);
  or or_46 (or_46_out, G[9], and_68_out);
  and and_69 (and_69_out, P[9], P[8]);
  or or_47 (Cout[8], and_70_out, or_56_out);
  and and_70 (and_70_out, Cin, and_84_out);
  and and_71 (and_71_out, and_60_out, or_56_out);
  or or_48 (or_48_out, or_40_out, and_71_out);
  and and_72 (and_72_out, and_60_out, and_84_out);
  or or_49 (Cout[7], and_73_out, G[6]);
  and and_73 (and_73_out, Cout[6], P[6]);
  or or_50 (or_50_out, G[7], and_74_out);
  and and_74 (and_74_out, P[7], G[6]);
  and and_75 (and_75_out, P[7], P[6]);
  or or_51 (Cout[6], and_76_out, or_54_out);
  and and_76 (and_76_out, Cout[4], and_81_out);
  and and_77 (and_77_out, and_75_out, or_54_out);
  or or_52 (or_52_out, or_50_out, and_77_out);
  and and_78 (and_78_out, and_75_out, and_81_out);
  or or_53 (Cout[5], and_79_out, G[4]);
  and and_79 (and_79_out, Cout[4], P[4]);
  and and_80 (and_80_out, P[5], G[4]);
  or or_54 (or_54_out, G[5], and_80_out);
  and and_81 (and_81_out, P[5], P[4]);
  or or_55 (Cout[4], and_82_out, or_60_out);
  and and_82 (and_82_out, Cin, and_90_out);
  or or_56 (or_56_out, or_52_out, and_83_out);
  and and_83 (and_83_out, and_78_out, or_60_out);
  and and_84 (and_84_out, and_78_out, and_90_out);
  or or_57 (Cout[3], and_85_out, G[2]);
  and and_85 (and_85_out, Cout[2], P[2]);
  and and_86 (and_86_out, P[3], G[2]);
  or or_58 (or_58_out, G[3], and_86_out);
  and and_87 (and_87_out, P[3], P[2]);
  or or_59 (Cout[2], and_88_out, or_62_out);
  and and_88 (and_88_out, Cin, and_93_out);
  and and_89 (and_89_out, and_87_out, or_62_out);
  or or_60 (or_60_out, or_58_out, and_89_out);
  and and_90 (and_90_out, and_87_out, and_93_out);
  or or_61 (Cout[1], and_91_out, G[0]);
  and and_91 (and_91_out, Cin, P[0]);
  and and_92 (and_92_out, P[1], G[0]);
  or or_62 (or_62_out, G[1], and_92_out);
  and and_93 (and_93_out, P[1], P[0]);

  assign Cout[0] = Cin;

  // Notes on the sheet:
  //   p1
  //   g1
  //   c1
  //   gout
  //   g0
  //   cin
  //   pout
  //   p1
  //   g1
  //   p0
  //   c0
  //   c1
  //   gout
  //   g1
  //   cin
  //   pout
  //   p1
  //   c1
  //   gout
  //   g0
  //   p0
  //   pout
  //   c0
  //   g0
  //   p0
  //   cin
  //   p1
  //   g1
  //   c0
  //   c1
  //   gout
  //   g1
  //   g0
  //   cin
  //   pout
  //   p1
  //   c1
  //   gout
  //   p0
  //   c0
  //   pout
  //   g1
  //   g0
  //   p0
  //   cin
  //   p1
  //   c1
  //   c0
  //   gout
  //   pout
  //   p1
  //   g1
  //   g0
  //   cin
  //   c1
  //   gout
  //   p0
  //   c0
  //   g0
  //   cin
  //   pout
  //   g1
  //   p0
  //   c0
  //   p1
  //   c1
  //   gout
  //   pout
  //   p1
  //   g1
  //   g0
  //   p0
  //   cin
  //   c1
  //   gout
  //   c0
  //   g0
  //   cin
  //   pout
  //   p1
  //   g1
  //   p0
  //   c0
  //   c1
  //   gout
  //   g1
  //   cin
  //   pout
  //   p1
  //   c1
  //   gout
  //   g0
  //   p0
  //   pout
  //   c0
  //   g0
  //   p0
  //   cin
  //   p1
  //   g1
  //   c0
  //   c1
  //   gout
  //   g1
  //   g0
  //   cin
  //   pout
  //   p1
  //   c1
  //   gout
  //   p0
  //   c0
  //   pout
  //   g1
  //   g0
  //   p0
  //   cin
  //   p1
  //   c1
  //   c0
  //   gout
  //   pout
  //   p1
  //   g1
  //   g0
  //   cin
  //   c1
  //   gout
  //   p0
  //   c0
  //   g0
  //   cin
  //   pout
  //   p0
  //   c0
  //   p1
  //   g1
  //   p1
  //   g1
  //   c1
  //   gout
  //   c1
  //   gout
  //   g0
  //   cin
  //   pout
  //   p1
  //   g1
  //   g0
  //   cin
  //   pout
  //   p0
  //   c0
  //   c1
  //   gout
  //   p0
  //   c0
  //   g1
  //   cin
  //   pout
  //   p1
  //   c1
  //   gout
  //   g0
  //   p0
  //   pout
  //   c0
  //   g0
  //   p0
  //   cin
  //   p1
  //   g1
  //   c0
  //   c1
  //   gout
  //   g1
  //   g0
  //   cin
  //   pout
  //   p1
  //   c1
  //   gout
  //   p0
  //   c0
  //   pout
  //   g1
  //   g0
  //   p0
  //   cin
  //   p1
  //   c1
  //   c0
  //   gout
  //   pout
  //   p1
  //   g1
  //   g0
  //   cin
  //   c1
  //   gout
  //   p0
  //   c0
  //   g0
  //   cin
  //   pout
  //   g1
  //   p0
  //   c0
  //   p1
  //   c1
  //   gout
  //   pout
  //   p1
  //   g1
  //   g0
  //   p0
  //   cin
  //   c1
  //   gout
  //   c0
  //   g0
  //   cin
  //   pout
  //   p1
  //   g1
  //   p0
  //   c0
  //   c1
  //   gout
  //   g1
  //   cin
  //   pout
  //   p1
  //   c1
  //   gout
  //   g0
  //   p0
  //   pout
  //   c0
  //   g0
  //   p0
  //   cin
  //   p1
  //   g1
  //   c0
  //   c1
  //   gout
  //   g1
  //   g0
  //   cin
  //   pout
  //   p1
  //   c1
  //   gout
  //   p0
  //   c0
  //   pout
  //   g1
  //   g0
  //   p0
  //   cin
  //   p1
  //   c1
  //   c0
  //   gout
  //   pout
  //   p1
  //   g1
  //   g0
  //   cin
  //   c1
  //   gout
  //   p0
  //   c0
  //   g0
  //   cin
  //   pout
  //   p0
  //   c0
endmodule

module ALU (
  input  [31:0] Abus,
  input  [31:0] Bbus,
  input  Cin,
  input  [2:0] Sel,
  output [31:0] Dbus,
  output Cout,
  output Zero,
  output Ovf
);

  wire and_1_out, lac32_1_gout, lac32_1_pout;
  wire [31:0] alubase_32_g, alubase_32_p, lac32_1_cout;

  and and_1 (and_1_out, Cin, lac32_1_pout);
  or or_1 (Cout, and_1_out, lac32_1_gout);
  LAC32 lac32_1 (
    .G(alubase_32_g), .P(alubase_32_p), .Cin(Cin), .Cout(lac32_1_cout), .gout(lac32_1_gout),
    .pout(lac32_1_pout));
  xor xor_1 (Ovf, Cout, lac32_1_cout[31]);
  ALUbase alubase_1 (
    .Sel(Sel), .A(Abus[31]), .B(Bbus[31]), .Cin(lac32_1_cout[31]), .sum(Dbus[31]), .g(alubase_32_g[31]),
    .p(alubase_32_p[31]));
  ALUbase alubase_2 (
    .Sel(Sel), .A(Abus[30]), .B(Bbus[30]), .Cin(lac32_1_cout[30]), .sum(Dbus[30]), .g(alubase_32_g[30]),
    .p(alubase_32_p[30]));
  ALUbase alubase_3 (
    .Sel(Sel), .A(Abus[29]), .B(Bbus[29]), .Cin(lac32_1_cout[29]), .sum(Dbus[29]), .g(alubase_32_g[29]),
    .p(alubase_32_p[29]));
  ALUbase alubase_4 (
    .Sel(Sel), .A(Abus[28]), .B(Bbus[28]), .Cin(lac32_1_cout[28]), .sum(Dbus[28]), .g(alubase_32_g[28]),
    .p(alubase_32_p[28]));
  ALUbase alubase_5 (
    .Sel(Sel), .A(Abus[27]), .B(Bbus[27]), .Cin(lac32_1_cout[27]), .sum(Dbus[27]), .g(alubase_32_g[27]),
    .p(alubase_32_p[27]));
  ALUbase alubase_6 (
    .Sel(Sel), .A(Abus[26]), .B(Bbus[26]), .Cin(lac32_1_cout[26]), .sum(Dbus[26]), .g(alubase_32_g[26]),
    .p(alubase_32_p[26]));
  nor nor_1 (Zero, Dbus[31], Dbus[30], Dbus[29], Dbus[28], Dbus[27], Dbus[26], Dbus[25], Dbus[24], Dbus[23], Dbus[22], Dbus[21], Dbus[20], Dbus[19], Dbus[18], Dbus[17], Dbus[16], Dbus[15], Dbus[14], Dbus[13], Dbus[12], Dbus[11], Dbus[10], Dbus[9], Dbus[8], Dbus[7], Dbus[6], Dbus[5], Dbus[4], Dbus[3], Dbus[2], Dbus[1], Dbus[0]);
  ALUbase alubase_7 (
    .Sel(Sel), .A(Abus[25]), .B(Bbus[25]), .Cin(lac32_1_cout[25]), .sum(Dbus[25]), .g(alubase_32_g[25]),
    .p(alubase_32_p[25]));
  ALUbase alubase_8 (
    .Sel(Sel), .A(Abus[24]), .B(Bbus[24]), .Cin(lac32_1_cout[24]), .sum(Dbus[24]), .g(alubase_32_g[24]),
    .p(alubase_32_p[24]));
  ALUbase alubase_9 (
    .Sel(Sel), .A(Abus[23]), .B(Bbus[23]), .Cin(lac32_1_cout[23]), .sum(Dbus[23]), .g(alubase_32_g[23]),
    .p(alubase_32_p[23]));
  ALUbase alubase_10 (
    .Sel(Sel), .A(Abus[22]), .B(Bbus[22]), .Cin(lac32_1_cout[22]), .sum(Dbus[22]), .g(alubase_32_g[22]),
    .p(alubase_32_p[22]));
  ALUbase alubase_11 (
    .Sel(Sel), .A(Abus[21]), .B(Bbus[21]), .Cin(lac32_1_cout[21]), .sum(Dbus[21]), .g(alubase_32_g[21]),
    .p(alubase_32_p[21]));
  ALUbase alubase_12 (
    .Sel(Sel), .A(Abus[20]), .B(Bbus[20]), .Cin(lac32_1_cout[20]), .sum(Dbus[20]), .g(alubase_32_g[20]),
    .p(alubase_32_p[20]));
  ALUbase alubase_13 (
    .Sel(Sel), .A(Abus[19]), .B(Bbus[19]), .Cin(lac32_1_cout[19]), .sum(Dbus[19]), .g(alubase_32_g[19]),
    .p(alubase_32_p[19]));
  ALUbase alubase_14 (
    .Sel(Sel), .A(Abus[18]), .B(Bbus[18]), .Cin(lac32_1_cout[18]), .sum(Dbus[18]), .g(alubase_32_g[18]),
    .p(alubase_32_p[18]));
  ALUbase alubase_15 (
    .Sel(Sel), .A(Abus[17]), .B(Bbus[17]), .Cin(lac32_1_cout[17]), .sum(Dbus[17]), .g(alubase_32_g[17]),
    .p(alubase_32_p[17]));
  ALUbase alubase_16 (
    .Sel(Sel), .A(Abus[16]), .B(Bbus[16]), .Cin(lac32_1_cout[16]), .sum(Dbus[16]), .g(alubase_32_g[16]),
    .p(alubase_32_p[16]));
  ALUbase alubase_17 (
    .Sel(Sel), .A(Abus[15]), .B(Bbus[15]), .Cin(lac32_1_cout[15]), .sum(Dbus[15]), .g(alubase_32_g[15]),
    .p(alubase_32_p[15]));
  ALUbase alubase_18 (
    .Sel(Sel), .A(Abus[14]), .B(Bbus[14]), .Cin(lac32_1_cout[14]), .sum(Dbus[14]), .g(alubase_32_g[14]),
    .p(alubase_32_p[14]));
  ALUbase alubase_19 (
    .Sel(Sel), .A(Abus[13]), .B(Bbus[13]), .Cin(lac32_1_cout[13]), .sum(Dbus[13]), .g(alubase_32_g[13]),
    .p(alubase_32_p[13]));
  ALUbase alubase_20 (
    .Sel(Sel), .A(Abus[12]), .B(Bbus[12]), .Cin(lac32_1_cout[12]), .sum(Dbus[12]), .g(alubase_32_g[12]),
    .p(alubase_32_p[12]));
  ALUbase alubase_21 (
    .Sel(Sel), .A(Abus[11]), .B(Bbus[11]), .Cin(lac32_1_cout[11]), .sum(Dbus[11]), .g(alubase_32_g[11]),
    .p(alubase_32_p[11]));
  ALUbase alubase_22 (
    .Sel(Sel), .A(Abus[10]), .B(Bbus[10]), .Cin(lac32_1_cout[10]), .sum(Dbus[10]), .g(alubase_32_g[10]),
    .p(alubase_32_p[10]));
  ALUbase alubase_23 (
    .Sel(Sel), .A(Abus[9]), .B(Bbus[9]), .Cin(lac32_1_cout[9]), .sum(Dbus[9]), .g(alubase_32_g[9]),
    .p(alubase_32_p[9]));
  ALUbase alubase_24 (
    .Sel(Sel), .A(Abus[8]), .B(Bbus[8]), .Cin(lac32_1_cout[8]), .sum(Dbus[8]), .g(alubase_32_g[8]),
    .p(alubase_32_p[8]));
  ALUbase alubase_25 (
    .Sel(Sel), .A(Abus[7]), .B(Bbus[7]), .Cin(lac32_1_cout[7]), .sum(Dbus[7]), .g(alubase_32_g[7]),
    .p(alubase_32_p[7]));
  ALUbase alubase_26 (
    .Sel(Sel), .A(Abus[6]), .B(Bbus[6]), .Cin(lac32_1_cout[6]), .sum(Dbus[6]), .g(alubase_32_g[6]),
    .p(alubase_32_p[6]));
  ALUbase alubase_27 (
    .Sel(Sel), .A(Abus[5]), .B(Bbus[5]), .Cin(lac32_1_cout[5]), .sum(Dbus[5]), .g(alubase_32_g[5]),
    .p(alubase_32_p[5]));
  ALUbase alubase_28 (
    .Sel(Sel), .A(Abus[4]), .B(Bbus[4]), .Cin(lac32_1_cout[4]), .sum(Dbus[4]), .g(alubase_32_g[4]),
    .p(alubase_32_p[4]));
  ALUbase alubase_29 (
    .Sel(Sel), .A(Abus[3]), .B(Bbus[3]), .Cin(lac32_1_cout[3]), .sum(Dbus[3]), .g(alubase_32_g[3]),
    .p(alubase_32_p[3]));
  ALUbase alubase_30 (
    .Sel(Sel), .A(Abus[2]), .B(Bbus[2]), .Cin(lac32_1_cout[2]), .sum(Dbus[2]), .g(alubase_32_g[2]),
    .p(alubase_32_p[2]));
  ALUbase alubase_31 (
    .Sel(Sel), .A(Abus[1]), .B(Bbus[1]), .Cin(lac32_1_cout[1]), .sum(Dbus[1]), .g(alubase_32_g[1]),
    .p(alubase_32_p[1]));
  ALUbase alubase_32 (
    .Sel(Sel), .A(Abus[0]), .B(Bbus[0]), .Cin(lac32_1_cout[0]), .sum(Dbus[0]), .g(alubase_32_g[0]),
    .p(alubase_32_p[0]));
endmodule

module ALUbase (
  input  [2:0] Sel,
  input  A,
  input  B,
  input  Cin,
  output sum,
  output g,
  output p
);

  wire and_2_out, nand_1_out, nor_1_out, or_1_out, xnor_1_out, xor_1_out, xor_3_out, xor_4_out, xor_5_out,
       xor_6_out, xor_7_out;

  xor xor_1 (xor_1_out, Sel[0], B);
  and and_1 (g, A, xor_1_out);
  xor xor_2 (p, A, xor_1_out);
  xor xor_3 (xor_3_out, A, B);
  or or_1 (or_1_out, A, B);
  and and_2 (and_2_out, A, B);
  nand nand_1 (nand_1_out, A, B);
  nor nor_1 (nor_1_out, B, A);
  xor xor_4 (xor_4_out, A, xor_1_out);
  xor xor_5 (xor_5_out, xor_4_out, Cin);
  xor xor_6 (xor_6_out, A, xor_1_out);
  xor xor_7 (xor_7_out, xor_6_out, Cin);
  xnor xnor_1 (xnor_1_out, A, B);
  Multiplexer #(.select(3)) multiplexer_1 (
    .in0(xor_3_out), .in1(or_1_out), .in2(xor_5_out), .in3(xor_7_out), .in4(and_2_out), .in5(nand_1_out),
    .in6(xnor_1_out), .in7(nor_1_out), .out(sum), .sel(Sel));
endmodule

module OpDecoder (
  input  [31:0] Ibus,
  output [31:0] Dsel,
  output IMM,
  output [2:0] Sel,
  output [31:0] Bsel,
  output [31:0] Asel,
  output LW,
  output SW,
  output Cin,
  output BEQ,
  output BNE,
  output JMP,
  output SHFT,
  output R_L,
  output [1:0] Sign,
  output [4:0] SHAMT
);

  wire and_1_out, and_2_out, and_3_out, and_4_out, nor_1_out, not_1_out, or_2_out, or_3_out;
  wire [2:0] and_6_out, and_9_out;
  wire [4:0] multiplexer_1_out;

  nor nor_1 (nor_1_out, Ibus[26], Ibus[27], Ibus[28], Ibus[29], Ibus[30], Ibus[31]);
  and and_1 (and_1_out, Ibus[4], Ibus[3]);
  or or_1 (IMM, Ibus[26], Ibus[27], Ibus[28], Ibus[29], Ibus[30], Ibus[31]);
  not not_1 (not_1_out, IMM);
  and and_2 (and_2_out, Ibus[26], ~Ibus[30]);  // AND_Gate
  or or_2 (or_2_out, Ibus[27], Ibus[30]);
  and and_3 (and_3_out, Ibus[0], Ibus[1], ~Ibus[2], ~Ibus[3], ~Ibus[4], Ibus[5]);  // AND_Gate
  and and_4 (and_4_out, Ibus[26], Ibus[27], ~Ibus[28], ~Ibus[29], ~Ibus[30], Ibus[31]);  // AND_Gate
  or or_3 (or_3_out, Ibus[3], Ibus[4]);
  and and_5 (Sign[1], and_1_out, nor_1_out);
  Multiplexer #(.width(5)) multiplexer_1 (.in0(Ibus[15:11]), .in1(Ibus[20:16]), .out(multiplexer_1_out), .sel(IMM));
  and and_6 (and_6_out[0], not_1_out, Ibus[0], Ibus[5]);
  and and_7 (and_6_out[1], not_1_out, Ibus[1], Ibus[5]);
  and and_8 (and_6_out[2], not_1_out, Ibus[2], Ibus[5]);
  and and_9 (and_9_out[0], IMM, Ibus[31], and_2_out);
  and and_10 (and_9_out[1], IMM, Ibus[31], or_2_out);
  and and_11 (and_9_out[2], IMM, Ibus[31], Ibus[28]);
  and and_12 (LW, Ibus[26], ~Ibus[27], ~Ibus[28], ~Ibus[29], Ibus[30], Ibus[31]);  // AND_Gate
  and and_13 (SW, ~Ibus[26], Ibus[27], ~Ibus[28], ~Ibus[29], Ibus[30], Ibus[31]);  // AND_Gate
  or or_4 (Cin, and_3_out, and_4_out);
  and and_14 (BEQ, ~Ibus[31], ~Ibus[30], Ibus[29], ~Ibus[28], ~Ibus[27], ~Ibus[26]);  // AND_Gate
  and and_15 (BNE, ~Ibus[31], ~Ibus[30], Ibus[29], Ibus[28], ~Ibus[27], ~Ibus[26]);  // AND_Gate
  and and_16 (JMP, Ibus[31], Ibus[30], Ibus[29], Ibus[28], Ibus[27], Ibus[26]);
  and and_17 (R_L, Ibus[4], nor_1_out);
  and and_18 (SHFT, or_3_out, nor_1_out);
  Multiplexer #(.width(3)) multiplexer_2 (.in0(and_6_out), .in1(and_9_out), .out(Sel), .sel(IMM));
  Decoder #(.enable("false"), .select(5)) decoder_1 (
    .out0(Dsel[0]), .out1(Dsel[1]), .out2(Dsel[2]), .out3(Dsel[3]), .out4(Dsel[4]), .out5(Dsel[5]),
    .out6(Dsel[6]), .out7(Dsel[7]), .out8(Dsel[8]), .out9(Dsel[9]), .out10(Dsel[10]), .out11(Dsel[11]),
    .out12(Dsel[12]), .out13(Dsel[13]), .out14(Dsel[14]), .out15(Dsel[15]), .out16(Dsel[16]),
    .out17(Dsel[17]), .out18(Dsel[18]), .out19(Dsel[19]), .out20(Dsel[20]), .out21(Dsel[21]),
    .out22(Dsel[22]), .out23(Dsel[23]), .out24(Dsel[24]), .out25(Dsel[25]), .out26(Dsel[26]),
    .out27(Dsel[27]), .out28(Dsel[28]), .out29(Dsel[29]), .out30(Dsel[30]), .out31(Dsel[31]),
    .sel(multiplexer_1_out));
  Decoder #(.enable("false"), .select(5)) decoder_2 (
    .out0(Bsel[0]), .out1(Bsel[1]), .out2(Bsel[2]), .out3(Bsel[3]), .out4(Bsel[4]), .out5(Bsel[5]),
    .out6(Bsel[6]), .out7(Bsel[7]), .out8(Bsel[8]), .out9(Bsel[9]), .out10(Bsel[10]), .out11(Bsel[11]),
    .out12(Bsel[12]), .out13(Bsel[13]), .out14(Bsel[14]), .out15(Bsel[15]), .out16(Bsel[16]),
    .out17(Bsel[17]), .out18(Bsel[18]), .out19(Bsel[19]), .out20(Bsel[20]), .out21(Bsel[21]),
    .out22(Bsel[22]), .out23(Bsel[23]), .out24(Bsel[24]), .out25(Bsel[25]), .out26(Bsel[26]),
    .out27(Bsel[27]), .out28(Bsel[28]), .out29(Bsel[29]), .out30(Bsel[30]), .out31(Bsel[31]),
    .sel(Ibus[20:16]));
  Decoder #(.enable("false"), .select(5)) decoder_3 (
    .out0(Asel[0]), .out1(Asel[1]), .out2(Asel[2]), .out3(Asel[3]), .out4(Asel[4]), .out5(Asel[5]),
    .out6(Asel[6]), .out7(Asel[7]), .out8(Asel[8]), .out9(Asel[9]), .out10(Asel[10]), .out11(Asel[11]),
    .out12(Asel[12]), .out13(Asel[13]), .out14(Asel[14]), .out15(Asel[15]), .out16(Asel[16]),
    .out17(Asel[17]), .out18(Asel[18]), .out19(Asel[19]), .out20(Asel[20]), .out21(Asel[21]),
    .out22(Asel[22]), .out23(Asel[23]), .out24(Asel[24]), .out25(Asel[25]), .out26(Asel[26]),
    .out27(Asel[27]), .out28(Asel[28]), .out29(Asel[29]), .out30(Asel[30]), .out31(Asel[31]),
    .sel(Ibus[25:21]));

  assign SHAMT = Ibus[10:6];
  assign Sign[0] = 1'b0;
endmodule

module Barrelshifter (
  input  [31:0] SHIN,
  input  [1:0] SIGN,
  input  [4:0] SHAMT,
  input  L_R,
  output [31:0] SHOUT
);

  wire multiplexer_2_out, multiplexer_3_out, multiplexer_4_out, multiplexer_5_out, multiplexer_6_out,
       multiplexer_7_out, multiplexer_8_out, multiplexer_9_out, multiplexer_10_out, multiplexer_11_out,
       multiplexer_12_out, multiplexer_13_out, multiplexer_14_out, multiplexer_15_out, multiplexer_16_out,
       multiplexer_17_out, multiplexer_18_out, multiplexer_19_out, multiplexer_20_out, multiplexer_21_out,
       multiplexer_22_out, multiplexer_23_out, multiplexer_24_out, multiplexer_25_out, multiplexer_26_out,
       multiplexer_27_out, multiplexer_28_out, multiplexer_29_out, multiplexer_30_out, multiplexer_31_out,
       multiplexer_32_out, multiplexer_33_out, multiplexer_34_out, multiplexer_35_out, multiplexer_36_out,
       multiplexer_37_out, multiplexer_38_out, multiplexer_39_out, multiplexer_40_out, multiplexer_41_out,
       multiplexer_42_out, multiplexer_43_out, multiplexer_44_out, multiplexer_45_out, multiplexer_46_out,
       multiplexer_47_out, multiplexer_48_out, multiplexer_49_out, multiplexer_50_out, multiplexer_51_out,
       multiplexer_52_out, multiplexer_53_out, multiplexer_54_out, multiplexer_55_out, multiplexer_56_out,
       multiplexer_57_out, multiplexer_58_out, multiplexer_59_out, multiplexer_60_out, multiplexer_61_out,
       multiplexer_62_out, multiplexer_63_out, multiplexer_64_out, multiplexer_65_out, multiplexer_66_out,
       multiplexer_67_out, multiplexer_68_out, multiplexer_69_out, multiplexer_70_out, multiplexer_71_out,
       multiplexer_72_out, multiplexer_73_out, multiplexer_74_out, multiplexer_75_out, multiplexer_76_out,
       multiplexer_77_out, multiplexer_78_out, multiplexer_79_out, multiplexer_80_out, multiplexer_81_out,
       multiplexer_82_out, multiplexer_83_out, multiplexer_84_out, multiplexer_85_out, multiplexer_86_out,
       multiplexer_87_out, multiplexer_88_out, multiplexer_89_out, multiplexer_90_out, multiplexer_91_out,
       multiplexer_92_out, multiplexer_93_out, multiplexer_94_out, multiplexer_95_out, multiplexer_96_out,
       multiplexer_97_out, multiplexer_98_out, multiplexer_99_out, multiplexer_100_out, multiplexer_101_out,
       multiplexer_102_out, multiplexer_103_out, multiplexer_104_out, multiplexer_105_out,
       multiplexer_106_out, multiplexer_107_out, multiplexer_108_out, multiplexer_109_out,
       multiplexer_110_out, multiplexer_111_out, multiplexer_112_out, multiplexer_113_out,
       multiplexer_114_out, multiplexer_115_out, multiplexer_116_out, multiplexer_117_out,
       multiplexer_118_out, multiplexer_119_out, multiplexer_120_out, multiplexer_121_out,
       multiplexer_122_out, multiplexer_123_out, multiplexer_124_out, multiplexer_125_out,
       multiplexer_126_out, multiplexer_127_out, multiplexer_128_out, multiplexer_129_out,
       multiplexer_130_out, multiplexer_131_out;
  wire [31:0] multiplexer_1_out, multiplexer_132_out;

  Multiplexer #(.width(32)) multiplexer_1 (
    .in0(SHIN),
    .in1({SHIN[0], SHIN[1], SHIN[2], SHIN[3], SHIN[4], SHIN[5], SHIN[6], SHIN[7], SHIN[8], SHIN[9], SHIN[10], SHIN[11], SHIN[12], SHIN[13], SHIN[14], SHIN[15], SHIN[16], SHIN[17], SHIN[18], SHIN[19], SHIN[20], SHIN[21], SHIN[22], SHIN[23], SHIN[24], SHIN[25], SHIN[26], SHIN[27], SHIN[28], SHIN[29], SHIN[30], SHIN[31]}),
    .out(multiplexer_1_out), .sel(L_R));
  Multiplexer #(.select(2)) multiplexer_2 (
    .in0(1'b0), .in1(1'b1), .in2(multiplexer_1_out[0]), .in3(1'b0), .out(multiplexer_2_out), .sel(SIGN));
  Multiplexer multiplexer_3 (.in0(1'b0), .in1(multiplexer_2_out), .out(multiplexer_3_out), .sel(L_R));
  Multiplexer multiplexer_4 (
    .in0(multiplexer_1_out[31]), .in1(multiplexer_1_out[30]), .out(multiplexer_4_out), .sel(SHAMT[0]));
  Multiplexer multiplexer_5 (
    .in0(multiplexer_1_out[30]), .in1(multiplexer_1_out[29]), .out(multiplexer_5_out), .sel(SHAMT[0]));
  Multiplexer multiplexer_6 (
    .in0(multiplexer_1_out[29]), .in1(multiplexer_1_out[28]), .out(multiplexer_6_out), .sel(SHAMT[0]));
  Multiplexer multiplexer_7 (
    .in0(multiplexer_1_out[28]), .in1(multiplexer_1_out[27]), .out(multiplexer_7_out), .sel(SHAMT[0]));
  Multiplexer multiplexer_8 (
    .in0(multiplexer_1_out[27]), .in1(multiplexer_1_out[26]), .out(multiplexer_8_out), .sel(SHAMT[0]));
  Multiplexer multiplexer_9 (
    .in0(multiplexer_1_out[26]), .in1(multiplexer_1_out[25]), .out(multiplexer_9_out), .sel(SHAMT[0]));
  Multiplexer multiplexer_10 (
    .in0(multiplexer_1_out[25]), .in1(multiplexer_1_out[24]), .out(multiplexer_10_out), .sel(SHAMT[0]));
  Multiplexer multiplexer_11 (
    .in0(multiplexer_1_out[24]), .in1(multiplexer_1_out[23]), .out(multiplexer_11_out), .sel(SHAMT[0]));
  Multiplexer multiplexer_12 (
    .in0(multiplexer_1_out[23]), .in1(multiplexer_1_out[22]), .out(multiplexer_12_out), .sel(SHAMT[0]));
  Multiplexer multiplexer_13 (
    .in0(multiplexer_1_out[22]), .in1(multiplexer_1_out[21]), .out(multiplexer_13_out), .sel(SHAMT[0]));
  Multiplexer multiplexer_14 (
    .in0(multiplexer_1_out[21]), .in1(multiplexer_1_out[20]), .out(multiplexer_14_out), .sel(SHAMT[0]));
  Multiplexer multiplexer_15 (
    .in0(multiplexer_1_out[20]), .in1(multiplexer_1_out[19]), .out(multiplexer_15_out), .sel(SHAMT[0]));
  Multiplexer multiplexer_16 (
    .in0(multiplexer_1_out[19]), .in1(multiplexer_1_out[18]), .out(multiplexer_16_out), .sel(SHAMT[0]));
  Multiplexer multiplexer_17 (
    .in0(multiplexer_1_out[18]), .in1(multiplexer_1_out[17]), .out(multiplexer_17_out), .sel(SHAMT[0]));
  Multiplexer multiplexer_18 (
    .in0(multiplexer_1_out[17]), .in1(multiplexer_1_out[16]), .out(multiplexer_18_out), .sel(SHAMT[0]));
  Multiplexer multiplexer_19 (
    .in0(multiplexer_1_out[16]), .in1(multiplexer_1_out[15]), .out(multiplexer_19_out), .sel(SHAMT[0]));
  Multiplexer multiplexer_20 (
    .in0(multiplexer_1_out[15]), .in1(multiplexer_1_out[14]), .out(multiplexer_20_out), .sel(SHAMT[0]));
  Multiplexer multiplexer_21 (
    .in0(multiplexer_1_out[14]), .in1(multiplexer_1_out[13]), .out(multiplexer_21_out), .sel(SHAMT[0]));
  Multiplexer multiplexer_22 (
    .in0(multiplexer_1_out[13]), .in1(multiplexer_1_out[12]), .out(multiplexer_22_out), .sel(SHAMT[0]));
  Multiplexer multiplexer_23 (
    .in0(multiplexer_1_out[12]), .in1(multiplexer_1_out[11]), .out(multiplexer_23_out), .sel(SHAMT[0]));
  Multiplexer multiplexer_24 (
    .in0(multiplexer_1_out[11]), .in1(multiplexer_1_out[10]), .out(multiplexer_24_out), .sel(SHAMT[0]));
  Multiplexer multiplexer_25 (
    .in0(multiplexer_1_out[10]), .in1(multiplexer_1_out[9]), .out(multiplexer_25_out), .sel(SHAMT[0]));
  Multiplexer multiplexer_26 (
    .in0(multiplexer_1_out[9]), .in1(multiplexer_1_out[8]), .out(multiplexer_26_out), .sel(SHAMT[0]));
  Multiplexer multiplexer_27 (
    .in0(multiplexer_1_out[8]), .in1(multiplexer_1_out[7]), .out(multiplexer_27_out), .sel(SHAMT[0]));
  Multiplexer multiplexer_28 (
    .in0(multiplexer_1_out[7]), .in1(multiplexer_1_out[6]), .out(multiplexer_28_out), .sel(SHAMT[0]));
  Multiplexer multiplexer_29 (
    .in0(multiplexer_1_out[6]), .in1(multiplexer_1_out[5]), .out(multiplexer_29_out), .sel(SHAMT[0]));
  Multiplexer multiplexer_30 (
    .in0(multiplexer_1_out[5]), .in1(multiplexer_1_out[4]), .out(multiplexer_30_out), .sel(SHAMT[0]));
  Multiplexer multiplexer_31 (
    .in0(multiplexer_1_out[4]), .in1(multiplexer_1_out[3]), .out(multiplexer_31_out), .sel(SHAMT[0]));
  Multiplexer multiplexer_32 (
    .in0(multiplexer_1_out[3]), .in1(multiplexer_1_out[2]), .out(multiplexer_32_out), .sel(SHAMT[0]));
  Multiplexer multiplexer_33 (
    .in0(multiplexer_1_out[2]), .in1(multiplexer_1_out[1]), .out(multiplexer_33_out), .sel(SHAMT[0]));
  Multiplexer multiplexer_34 (
    .in0(multiplexer_1_out[1]), .in1(multiplexer_1_out[0]), .out(multiplexer_34_out), .sel(SHAMT[0]));
  Multiplexer multiplexer_35 (
    .in0(multiplexer_1_out[0]), .in1(multiplexer_3_out), .out(multiplexer_35_out), .sel(SHAMT[0]));
  Multiplexer multiplexer_36 (
    .in0(multiplexer_4_out), .in1(multiplexer_6_out), .out(multiplexer_36_out), .sel(SHAMT[1]));
  Multiplexer multiplexer_37 (
    .in0(multiplexer_5_out), .in1(multiplexer_7_out), .out(multiplexer_37_out), .sel(SHAMT[1]));
  Multiplexer multiplexer_38 (
    .in0(multiplexer_6_out), .in1(multiplexer_8_out), .out(multiplexer_38_out), .sel(SHAMT[1]));
  Multiplexer multiplexer_39 (
    .in0(multiplexer_7_out), .in1(multiplexer_9_out), .out(multiplexer_39_out), .sel(SHAMT[1]));
  Multiplexer multiplexer_40 (
    .in0(multiplexer_8_out), .in1(multiplexer_10_out), .out(multiplexer_40_out), .sel(SHAMT[1]));
  Multiplexer multiplexer_41 (
    .in0(multiplexer_9_out), .in1(multiplexer_11_out), .out(multiplexer_41_out), .sel(SHAMT[1]));
  Multiplexer multiplexer_42 (
    .in0(multiplexer_10_out), .in1(multiplexer_12_out), .out(multiplexer_42_out), .sel(SHAMT[1]));
  Multiplexer multiplexer_43 (
    .in0(multiplexer_11_out), .in1(multiplexer_13_out), .out(multiplexer_43_out), .sel(SHAMT[1]));
  Multiplexer multiplexer_44 (
    .in0(multiplexer_12_out), .in1(multiplexer_14_out), .out(multiplexer_44_out), .sel(SHAMT[1]));
  Multiplexer multiplexer_45 (
    .in0(multiplexer_13_out), .in1(multiplexer_15_out), .out(multiplexer_45_out), .sel(SHAMT[1]));
  Multiplexer multiplexer_46 (
    .in0(multiplexer_14_out), .in1(multiplexer_16_out), .out(multiplexer_46_out), .sel(SHAMT[1]));
  Multiplexer multiplexer_47 (
    .in0(multiplexer_15_out), .in1(multiplexer_17_out), .out(multiplexer_47_out), .sel(SHAMT[1]));
  Multiplexer multiplexer_48 (
    .in0(multiplexer_16_out), .in1(multiplexer_18_out), .out(multiplexer_48_out), .sel(SHAMT[1]));
  Multiplexer multiplexer_49 (
    .in0(multiplexer_17_out), .in1(multiplexer_19_out), .out(multiplexer_49_out), .sel(SHAMT[1]));
  Multiplexer multiplexer_50 (
    .in0(multiplexer_18_out), .in1(multiplexer_20_out), .out(multiplexer_50_out), .sel(SHAMT[1]));
  Multiplexer multiplexer_51 (
    .in0(multiplexer_19_out), .in1(multiplexer_21_out), .out(multiplexer_51_out), .sel(SHAMT[1]));
  Multiplexer multiplexer_52 (
    .in0(multiplexer_20_out), .in1(multiplexer_22_out), .out(multiplexer_52_out), .sel(SHAMT[1]));
  Multiplexer multiplexer_53 (
    .in0(multiplexer_21_out), .in1(multiplexer_23_out), .out(multiplexer_53_out), .sel(SHAMT[1]));
  Multiplexer multiplexer_54 (
    .in0(multiplexer_22_out), .in1(multiplexer_24_out), .out(multiplexer_54_out), .sel(SHAMT[1]));
  Multiplexer multiplexer_55 (
    .in0(multiplexer_23_out), .in1(multiplexer_25_out), .out(multiplexer_55_out), .sel(SHAMT[1]));
  Multiplexer multiplexer_56 (
    .in0(multiplexer_24_out), .in1(multiplexer_26_out), .out(multiplexer_56_out), .sel(SHAMT[1]));
  Multiplexer multiplexer_57 (
    .in0(multiplexer_25_out), .in1(multiplexer_27_out), .out(multiplexer_57_out), .sel(SHAMT[1]));
  Multiplexer multiplexer_58 (
    .in0(multiplexer_26_out), .in1(multiplexer_28_out), .out(multiplexer_58_out), .sel(SHAMT[1]));
  Multiplexer multiplexer_59 (
    .in0(multiplexer_27_out), .in1(multiplexer_29_out), .out(multiplexer_59_out), .sel(SHAMT[1]));
  Multiplexer multiplexer_60 (
    .in0(multiplexer_28_out), .in1(multiplexer_30_out), .out(multiplexer_60_out), .sel(SHAMT[1]));
  Multiplexer multiplexer_61 (
    .in0(multiplexer_29_out), .in1(multiplexer_31_out), .out(multiplexer_61_out), .sel(SHAMT[1]));
  Multiplexer multiplexer_62 (
    .in0(multiplexer_30_out), .in1(multiplexer_32_out), .out(multiplexer_62_out), .sel(SHAMT[1]));
  Multiplexer multiplexer_63 (
    .in0(multiplexer_31_out), .in1(multiplexer_33_out), .out(multiplexer_63_out), .sel(SHAMT[1]));
  Multiplexer multiplexer_64 (
    .in0(multiplexer_32_out), .in1(multiplexer_34_out), .out(multiplexer_64_out), .sel(SHAMT[1]));
  Multiplexer multiplexer_65 (
    .in0(multiplexer_33_out), .in1(multiplexer_35_out), .out(multiplexer_65_out), .sel(SHAMT[1]));
  Multiplexer multiplexer_66 (
    .in0(multiplexer_34_out), .in1(multiplexer_3_out), .out(multiplexer_66_out), .sel(SHAMT[1]));
  Multiplexer multiplexer_67 (
    .in0(multiplexer_35_out), .in1(multiplexer_3_out), .out(multiplexer_67_out), .sel(SHAMT[1]));
  Multiplexer multiplexer_68 (
    .in0(multiplexer_36_out), .in1(multiplexer_40_out), .out(multiplexer_68_out), .sel(SHAMT[2]));
  Multiplexer multiplexer_69 (
    .in0(multiplexer_37_out), .in1(multiplexer_41_out), .out(multiplexer_69_out), .sel(SHAMT[2]));
  Multiplexer multiplexer_70 (
    .in0(multiplexer_38_out), .in1(multiplexer_42_out), .out(multiplexer_70_out), .sel(SHAMT[2]));
  Multiplexer multiplexer_71 (
    .in0(multiplexer_39_out), .in1(multiplexer_43_out), .out(multiplexer_71_out), .sel(SHAMT[2]));
  Multiplexer multiplexer_72 (
    .in0(multiplexer_40_out), .in1(multiplexer_44_out), .out(multiplexer_72_out), .sel(SHAMT[2]));
  Multiplexer multiplexer_73 (
    .in0(multiplexer_41_out), .in1(multiplexer_45_out), .out(multiplexer_73_out), .sel(SHAMT[2]));
  Multiplexer multiplexer_74 (
    .in0(multiplexer_42_out), .in1(multiplexer_46_out), .out(multiplexer_74_out), .sel(SHAMT[2]));
  Multiplexer multiplexer_75 (
    .in0(multiplexer_43_out), .in1(multiplexer_47_out), .out(multiplexer_75_out), .sel(SHAMT[2]));
  Multiplexer multiplexer_76 (
    .in0(multiplexer_44_out), .in1(multiplexer_48_out), .out(multiplexer_76_out), .sel(SHAMT[2]));
  Multiplexer multiplexer_77 (
    .in0(multiplexer_45_out), .in1(multiplexer_49_out), .out(multiplexer_77_out), .sel(SHAMT[2]));
  Multiplexer multiplexer_78 (
    .in0(multiplexer_46_out), .in1(multiplexer_50_out), .out(multiplexer_78_out), .sel(SHAMT[2]));
  Multiplexer multiplexer_79 (
    .in0(multiplexer_47_out), .in1(multiplexer_51_out), .out(multiplexer_79_out), .sel(SHAMT[2]));
  Multiplexer multiplexer_80 (
    .in0(multiplexer_48_out), .in1(multiplexer_52_out), .out(multiplexer_80_out), .sel(SHAMT[2]));
  Multiplexer multiplexer_81 (
    .in0(multiplexer_49_out), .in1(multiplexer_53_out), .out(multiplexer_81_out), .sel(SHAMT[2]));
  Multiplexer multiplexer_82 (
    .in0(multiplexer_50_out), .in1(multiplexer_54_out), .out(multiplexer_82_out), .sel(SHAMT[2]));
  Multiplexer multiplexer_83 (
    .in0(multiplexer_51_out), .in1(multiplexer_55_out), .out(multiplexer_83_out), .sel(SHAMT[2]));
  Multiplexer multiplexer_84 (
    .in0(multiplexer_52_out), .in1(multiplexer_56_out), .out(multiplexer_84_out), .sel(SHAMT[2]));
  Multiplexer multiplexer_85 (
    .in0(multiplexer_53_out), .in1(multiplexer_57_out), .out(multiplexer_85_out), .sel(SHAMT[2]));
  Multiplexer multiplexer_86 (
    .in0(multiplexer_54_out), .in1(multiplexer_58_out), .out(multiplexer_86_out), .sel(SHAMT[2]));
  Multiplexer multiplexer_87 (
    .in0(multiplexer_55_out), .in1(multiplexer_59_out), .out(multiplexer_87_out), .sel(SHAMT[2]));
  Multiplexer multiplexer_88 (
    .in0(multiplexer_56_out), .in1(multiplexer_60_out), .out(multiplexer_88_out), .sel(SHAMT[2]));
  Multiplexer multiplexer_89 (
    .in0(multiplexer_57_out), .in1(multiplexer_61_out), .out(multiplexer_89_out), .sel(SHAMT[2]));
  Multiplexer multiplexer_90 (
    .in0(multiplexer_58_out), .in1(multiplexer_62_out), .out(multiplexer_90_out), .sel(SHAMT[2]));
  Multiplexer multiplexer_91 (
    .in0(multiplexer_59_out), .in1(multiplexer_63_out), .out(multiplexer_91_out), .sel(SHAMT[2]));
  Multiplexer multiplexer_92 (
    .in0(multiplexer_60_out), .in1(multiplexer_64_out), .out(multiplexer_92_out), .sel(SHAMT[2]));
  Multiplexer multiplexer_93 (
    .in0(multiplexer_61_out), .in1(multiplexer_65_out), .out(multiplexer_93_out), .sel(SHAMT[2]));
  Multiplexer multiplexer_94 (
    .in0(multiplexer_62_out), .in1(multiplexer_66_out), .out(multiplexer_94_out), .sel(SHAMT[2]));
  Multiplexer multiplexer_95 (
    .in0(multiplexer_63_out), .in1(multiplexer_67_out), .out(multiplexer_95_out), .sel(SHAMT[2]));
  Multiplexer multiplexer_96 (
    .in0(multiplexer_64_out), .in1(multiplexer_3_out), .out(multiplexer_96_out), .sel(SHAMT[2]));
  Multiplexer multiplexer_97 (
    .in0(multiplexer_65_out), .in1(multiplexer_3_out), .out(multiplexer_97_out), .sel(SHAMT[2]));
  Multiplexer multiplexer_98 (
    .in0(multiplexer_66_out), .in1(multiplexer_3_out), .out(multiplexer_98_out), .sel(SHAMT[2]));
  Multiplexer multiplexer_99 (
    .in0(multiplexer_67_out), .in1(multiplexer_3_out), .out(multiplexer_99_out), .sel(SHAMT[2]));
  Multiplexer multiplexer_100 (
    .in0(multiplexer_68_out), .in1(multiplexer_76_out), .out(multiplexer_100_out), .sel(SHAMT[3]));
  Multiplexer multiplexer_101 (
    .in0(multiplexer_69_out), .in1(multiplexer_77_out), .out(multiplexer_101_out), .sel(SHAMT[3]));
  Multiplexer multiplexer_102 (
    .in0(multiplexer_70_out), .in1(multiplexer_78_out), .out(multiplexer_102_out), .sel(SHAMT[3]));
  Multiplexer multiplexer_103 (
    .in0(multiplexer_71_out), .in1(multiplexer_79_out), .out(multiplexer_103_out), .sel(SHAMT[3]));
  Multiplexer multiplexer_104 (
    .in0(multiplexer_72_out), .in1(multiplexer_80_out), .out(multiplexer_104_out), .sel(SHAMT[3]));
  Multiplexer multiplexer_105 (
    .in0(multiplexer_73_out), .in1(multiplexer_81_out), .out(multiplexer_105_out), .sel(SHAMT[3]));
  Multiplexer multiplexer_106 (
    .in0(multiplexer_74_out), .in1(multiplexer_82_out), .out(multiplexer_106_out), .sel(SHAMT[3]));
  Multiplexer multiplexer_107 (
    .in0(multiplexer_75_out), .in1(multiplexer_83_out), .out(multiplexer_107_out), .sel(SHAMT[3]));
  Multiplexer multiplexer_108 (
    .in0(multiplexer_76_out), .in1(multiplexer_84_out), .out(multiplexer_108_out), .sel(SHAMT[3]));
  Multiplexer multiplexer_109 (
    .in0(multiplexer_77_out), .in1(multiplexer_85_out), .out(multiplexer_109_out), .sel(SHAMT[3]));
  Multiplexer multiplexer_110 (
    .in0(multiplexer_78_out), .in1(multiplexer_86_out), .out(multiplexer_110_out), .sel(SHAMT[3]));
  Multiplexer multiplexer_111 (
    .in0(multiplexer_79_out), .in1(multiplexer_87_out), .out(multiplexer_111_out), .sel(SHAMT[3]));
  Multiplexer multiplexer_112 (
    .in0(multiplexer_80_out), .in1(multiplexer_88_out), .out(multiplexer_112_out), .sel(SHAMT[3]));
  Multiplexer multiplexer_113 (
    .in0(multiplexer_81_out), .in1(multiplexer_89_out), .out(multiplexer_113_out), .sel(SHAMT[3]));
  Multiplexer multiplexer_114 (
    .in0(multiplexer_82_out), .in1(multiplexer_90_out), .out(multiplexer_114_out), .sel(SHAMT[3]));
  Multiplexer multiplexer_115 (
    .in0(multiplexer_83_out), .in1(multiplexer_91_out), .out(multiplexer_115_out), .sel(SHAMT[3]));
  Multiplexer multiplexer_116 (
    .in0(multiplexer_84_out), .in1(multiplexer_92_out), .out(multiplexer_116_out), .sel(SHAMT[3]));
  Multiplexer multiplexer_117 (
    .in0(multiplexer_85_out), .in1(multiplexer_93_out), .out(multiplexer_117_out), .sel(SHAMT[3]));
  Multiplexer multiplexer_118 (
    .in0(multiplexer_86_out), .in1(multiplexer_94_out), .out(multiplexer_118_out), .sel(SHAMT[3]));
  Multiplexer multiplexer_119 (
    .in0(multiplexer_87_out), .in1(multiplexer_95_out), .out(multiplexer_119_out), .sel(SHAMT[3]));
  Multiplexer multiplexer_120 (
    .in0(multiplexer_88_out), .in1(multiplexer_96_out), .out(multiplexer_120_out), .sel(SHAMT[3]));
  Multiplexer multiplexer_121 (
    .in0(multiplexer_89_out), .in1(multiplexer_97_out), .out(multiplexer_121_out), .sel(SHAMT[3]));
  Multiplexer multiplexer_122 (
    .in0(multiplexer_90_out), .in1(multiplexer_98_out), .out(multiplexer_122_out), .sel(SHAMT[3]));
  Multiplexer multiplexer_123 (
    .in0(multiplexer_91_out), .in1(multiplexer_99_out), .out(multiplexer_123_out), .sel(SHAMT[3]));
  Multiplexer multiplexer_124 (
    .in0(multiplexer_92_out), .in1(multiplexer_3_out), .out(multiplexer_124_out), .sel(SHAMT[3]));
  Multiplexer multiplexer_125 (
    .in0(multiplexer_93_out), .in1(multiplexer_3_out), .out(multiplexer_125_out), .sel(SHAMT[3]));
  Multiplexer multiplexer_126 (
    .in0(multiplexer_94_out), .in1(multiplexer_3_out), .out(multiplexer_126_out), .sel(SHAMT[3]));
  Multiplexer multiplexer_127 (
    .in0(multiplexer_95_out), .in1(multiplexer_3_out), .out(multiplexer_127_out), .sel(SHAMT[3]));
  Multiplexer multiplexer_128 (
    .in0(multiplexer_96_out), .in1(multiplexer_3_out), .out(multiplexer_128_out), .sel(SHAMT[3]));
  Multiplexer multiplexer_129 (
    .in0(multiplexer_97_out), .in1(multiplexer_3_out), .out(multiplexer_129_out), .sel(SHAMT[3]));
  Multiplexer multiplexer_130 (
    .in0(multiplexer_98_out), .in1(multiplexer_3_out), .out(multiplexer_130_out), .sel(SHAMT[3]));
  Multiplexer multiplexer_131 (
    .in0(multiplexer_99_out), .in1(multiplexer_3_out), .out(multiplexer_131_out), .sel(SHAMT[3]));
  Multiplexer multiplexer_132 (
    .in0(multiplexer_100_out), .in1(multiplexer_116_out), .out(multiplexer_132_out[31]), .sel(SHAMT[4]));
  Multiplexer multiplexer_133 (
    .in0(multiplexer_101_out), .in1(multiplexer_117_out), .out(multiplexer_132_out[30]), .sel(SHAMT[4]));
  Multiplexer multiplexer_134 (
    .in0(multiplexer_102_out), .in1(multiplexer_118_out), .out(multiplexer_132_out[29]), .sel(SHAMT[4]));
  Multiplexer multiplexer_135 (
    .in0(multiplexer_103_out), .in1(multiplexer_119_out), .out(multiplexer_132_out[28]), .sel(SHAMT[4]));
  Multiplexer multiplexer_136 (
    .in0(multiplexer_104_out), .in1(multiplexer_120_out), .out(multiplexer_132_out[27]), .sel(SHAMT[4]));
  Multiplexer multiplexer_137 (
    .in0(multiplexer_105_out), .in1(multiplexer_121_out), .out(multiplexer_132_out[26]), .sel(SHAMT[4]));
  Multiplexer multiplexer_138 (
    .in0(multiplexer_106_out), .in1(multiplexer_122_out), .out(multiplexer_132_out[25]), .sel(SHAMT[4]));
  Multiplexer multiplexer_139 (
    .in0(multiplexer_107_out), .in1(multiplexer_123_out), .out(multiplexer_132_out[24]), .sel(SHAMT[4]));
  Multiplexer multiplexer_140 (
    .in0(multiplexer_108_out), .in1(multiplexer_124_out), .out(multiplexer_132_out[23]), .sel(SHAMT[4]));
  Multiplexer multiplexer_141 (
    .in0(multiplexer_109_out), .in1(multiplexer_125_out), .out(multiplexer_132_out[22]), .sel(SHAMT[4]));
  Multiplexer multiplexer_142 (
    .in0(multiplexer_110_out), .in1(multiplexer_126_out), .out(multiplexer_132_out[21]), .sel(SHAMT[4]));
  Multiplexer multiplexer_143 (
    .in0(multiplexer_111_out), .in1(multiplexer_127_out), .out(multiplexer_132_out[20]), .sel(SHAMT[4]));
  Multiplexer multiplexer_144 (
    .in0(multiplexer_112_out), .in1(multiplexer_128_out), .out(multiplexer_132_out[19]), .sel(SHAMT[4]));
  Multiplexer multiplexer_145 (
    .in0(multiplexer_113_out), .in1(multiplexer_129_out), .out(multiplexer_132_out[18]), .sel(SHAMT[4]));
  Multiplexer multiplexer_146 (
    .in0(multiplexer_114_out), .in1(multiplexer_130_out), .out(multiplexer_132_out[17]), .sel(SHAMT[4]));
  Multiplexer multiplexer_147 (
    .in0(multiplexer_115_out), .in1(multiplexer_131_out), .out(multiplexer_132_out[16]), .sel(SHAMT[4]));
  Multiplexer multiplexer_148 (
    .in0(multiplexer_116_out), .in1(multiplexer_3_out), .out(multiplexer_132_out[15]), .sel(SHAMT[4]));
  Multiplexer multiplexer_149 (
    .in0(multiplexer_117_out), .in1(multiplexer_3_out), .out(multiplexer_132_out[14]), .sel(SHAMT[4]));
  Multiplexer multiplexer_150 (
    .in0(multiplexer_118_out), .in1(multiplexer_3_out), .out(multiplexer_132_out[13]), .sel(SHAMT[4]));
  Multiplexer multiplexer_151 (
    .in0(multiplexer_119_out), .in1(multiplexer_3_out), .out(multiplexer_132_out[12]), .sel(SHAMT[4]));
  Multiplexer multiplexer_152 (
    .in0(multiplexer_120_out), .in1(multiplexer_3_out), .out(multiplexer_132_out[11]), .sel(SHAMT[4]));
  Multiplexer multiplexer_153 (
    .in0(multiplexer_121_out), .in1(multiplexer_3_out), .out(multiplexer_132_out[10]), .sel(SHAMT[4]));
  Multiplexer multiplexer_154 (
    .in0(multiplexer_122_out), .in1(multiplexer_3_out), .out(multiplexer_132_out[9]), .sel(SHAMT[4]));
  Multiplexer multiplexer_155 (
    .in0(multiplexer_123_out), .in1(multiplexer_3_out), .out(multiplexer_132_out[8]), .sel(SHAMT[4]));
  Multiplexer multiplexer_156 (
    .in0(multiplexer_124_out), .in1(multiplexer_3_out), .out(multiplexer_132_out[7]), .sel(SHAMT[4]));
  Multiplexer multiplexer_157 (
    .in0(multiplexer_125_out), .in1(multiplexer_3_out), .out(multiplexer_132_out[6]), .sel(SHAMT[4]));
  Multiplexer multiplexer_158 (
    .in0(multiplexer_126_out), .in1(multiplexer_3_out), .out(multiplexer_132_out[5]), .sel(SHAMT[4]));
  Multiplexer multiplexer_159 (
    .in0(multiplexer_127_out), .in1(multiplexer_3_out), .out(multiplexer_132_out[4]), .sel(SHAMT[4]));
  Multiplexer multiplexer_160 (
    .in0(multiplexer_128_out), .in1(multiplexer_3_out), .out(multiplexer_132_out[3]), .sel(SHAMT[4]));
  Multiplexer multiplexer_161 (
    .in0(multiplexer_129_out), .in1(multiplexer_3_out), .out(multiplexer_132_out[2]), .sel(SHAMT[4]));
  Multiplexer multiplexer_162 (
    .in0(multiplexer_130_out), .in1(multiplexer_3_out), .out(multiplexer_132_out[1]), .sel(SHAMT[4]));
  Multiplexer multiplexer_163 (
    .in0(multiplexer_131_out), .in1(multiplexer_3_out), .out(multiplexer_132_out[0]), .sel(SHAMT[4]));
  Multiplexer #(.width(32)) multiplexer_164 (
    .in0(multiplexer_132_out),
    .in1({multiplexer_132_out[0], multiplexer_132_out[1], multiplexer_132_out[2], multiplexer_132_out[3], multiplexer_132_out[4], multiplexer_132_out[5], multiplexer_132_out[6], multiplexer_132_out[7], multiplexer_132_out[8], multiplexer_132_out[9], multiplexer_132_out[10], multiplexer_132_out[11], multiplexer_132_out[12], multiplexer_132_out[13], multiplexer_132_out[14], multiplexer_132_out[15], multiplexer_132_out[16], multiplexer_132_out[17], multiplexer_132_out[18], multiplexer_132_out[19], multiplexer_132_out[20], multiplexer_132_out[21], multiplexer_132_out[22], multiplexer_132_out[23], multiplexer_132_out[24], multiplexer_132_out[25], multiplexer_132_out[26], multiplexer_132_out[27], multiplexer_132_out[28], multiplexer_132_out[29], multiplexer_132_out[30], multiplexer_132_out[31]}),
    .out(SHOUT), .sel(L_R));
endmodule

module Comp (
  input  [31:0] in_1,
  input  [31:0] in_2,
  output out_3
);

  wire xnor_1_out, xnor_2_out, xnor_3_out, xnor_4_out, xnor_5_out, xnor_6_out, xnor_7_out, xnor_8_out,
       xnor_9_out, xnor_10_out, xnor_11_out, xnor_12_out, xnor_13_out, xnor_14_out, xnor_15_out, xnor_16_out,
       xnor_17_out, xnor_18_out, xnor_19_out, xnor_20_out, xnor_21_out, xnor_22_out, xnor_23_out,
       xnor_24_out, xnor_25_out, xnor_26_out, xnor_27_out, xnor_28_out, xnor_29_out, xnor_30_out,
       xnor_31_out, xnor_32_out;

  xnor xnor_1 (xnor_1_out, in_1[0], in_2[0]);
  xnor xnor_2 (xnor_2_out, in_1[1], in_2[1]);
  xnor xnor_3 (xnor_3_out, in_1[2], in_2[2]);
  xnor xnor_4 (xnor_4_out, in_1[3], in_2[3]);
  xnor xnor_5 (xnor_5_out, in_1[4], in_2[4]);
  xnor xnor_6 (xnor_6_out, in_1[5], in_2[5]);
  xnor xnor_7 (xnor_7_out, in_1[6], in_2[6]);
  xnor xnor_8 (xnor_8_out, in_1[7], in_2[7]);
  xnor xnor_9 (xnor_9_out, in_1[8], in_2[8]);
  xnor xnor_10 (xnor_10_out, in_1[9], in_2[9]);
  xnor xnor_11 (xnor_11_out, in_1[10], in_2[10]);
  xnor xnor_12 (xnor_12_out, in_1[11], in_2[11]);
  xnor xnor_13 (xnor_13_out, in_1[12], in_2[12]);
  xnor xnor_14 (xnor_14_out, in_1[13], in_2[13]);
  xnor xnor_15 (xnor_15_out, in_1[14], in_2[14]);
  xnor xnor_16 (xnor_16_out, in_1[15], in_2[15]);
  xnor xnor_17 (xnor_17_out, in_1[16], in_2[16]);
  xnor xnor_18 (xnor_18_out, in_1[17], in_2[17]);
  xnor xnor_19 (xnor_19_out, in_1[18], in_2[18]);
  xnor xnor_20 (xnor_20_out, in_1[19], in_2[19]);
  xnor xnor_21 (xnor_21_out, in_1[20], in_2[20]);
  xnor xnor_22 (xnor_22_out, in_1[21], in_2[21]);
  xnor xnor_23 (xnor_23_out, in_1[22], in_2[22]);
  xnor xnor_24 (xnor_24_out, in_1[23], in_2[23]);
  xnor xnor_25 (xnor_25_out, in_1[24], in_2[24]);
  xnor xnor_26 (xnor_26_out, in_1[25], in_2[25]);
  xnor xnor_27 (xnor_27_out, in_1[26], in_2[26]);
  xnor xnor_28 (xnor_28_out, in_1[27], in_2[27]);
  xnor xnor_29 (xnor_29_out, in_1[28], in_2[28]);
  xnor xnor_30 (xnor_30_out, in_1[29], in_2[29]);
  xnor xnor_31 (xnor_31_out, in_1[30], in_2[30]);
  xnor xnor_32 (xnor_32_out, in_1[31], in_2[31]);
  and and_1 (out_3, xnor_1_out, xnor_2_out, xnor_3_out, xnor_4_out, xnor_5_out, xnor_6_out, xnor_7_out, xnor_8_out, xnor_9_out, xnor_10_out, xnor_11_out, xnor_12_out, xnor_13_out, xnor_14_out, xnor_15_out, xnor_16_out, xnor_17_out, xnor_18_out, xnor_19_out, xnor_20_out, xnor_21_out, xnor_22_out, xnor_23_out, xnor_24_out, xnor_25_out, xnor_26_out, xnor_27_out, xnor_28_out, xnor_29_out, xnor_30_out, xnor_31_out, xnor_32_out);
endmodule

module Extend (
  input  [31:0] in_1,
  output [31:0] out_2
);


  assign out_2 = {{17{in_1[15]}}, in_1[14:0]};
endmodule

module b3224 (
  input  [31:0] in_1,
  output [23:0] out_2
);


  assign out_2 = in_1[23:0];
endmodule

module Retractor (
  input  [31:0] in_1,
  output [31:0] out_2
);


  assign out_2 = {{6{1'b0}}, in_1[25:0]};
endmodule

module TEST (
  input  in_1,
  input  [7:0] in_2,
  output [7:0] out_3
);

  Register #(.trigger("falling")) register_1 (.D(in_2), .en(1'b1), .clk(in_1), .Q(out_3));  // open: clr
endmodule
